// Logisim project WolfCPU.circ as structural Verilog: 1 circuit, main circuit main
module main (
  input  in_1,
  input  in_2,
  input  in_3,
  input  in_4,
  input  in_5,
  input  in_6,
  input  in_7,
  input  in_8,
  input  in_9
);

  wire clock_1_out, not_1_out;
  wire [7:0] adder_1_out, controlled_buffer_1_out, Instruction_q, Microcode_Counter_q, Program_Counter_q,
       RAM_Register_q, Register_A_q, Register_B_q;
  wire [31:0] rom_1_data;

  Counter Microcode_Counter (
    .Q(Microcode_Counter_q), .clk(not_1_out), .clr(rom_1_data[4]));  // open: load, D, count, carry
  Register Instruction (
    .D(controlled_buffer_1_out), .en(rom_1_data[8]), .Q(Instruction_q), .clk(not_1_out));  // open: clr
  Clock clock_1 (.out(clock_1_out));
  not not_1 (not_1_out, clock_1_out);
  ROM #(.addrWidth(16), .dataWidth(32)) rom_1 (
    .addr({Microcode_Counter_q, Instruction_q}), .data(rom_1_data));  // open: sel
  // Probe on controlled_buffer_1_out
  assign controlled_buffer_1_out = rom_1_data[1] ? Register_A_q : 8'bz;  // Controlled_Buffer controlled_buffer_1
  Register Register_A (
    .D(controlled_buffer_1_out), .en(rom_1_data[0]), .Q(Register_A_q), .clk(clock_1_out));  // open: clr
  Register Register_B (
    .D(controlled_buffer_1_out), .en(rom_1_data[2]), .Q(Register_B_q), .clk(clock_1_out));  // open: clr
  assign controlled_buffer_1_out = rom_1_data[3] ? Register_B_q : 8'bz;  // Controlled_Buffer controlled_buffer_2
  Adder adder_1 (.a(Register_B_q), .b(Register_A_q), .out(adder_1_out));  // open: cin, cout
  assign controlled_buffer_1_out = rom_1_data[4] ? adder_1_out : 8'bz;  // Controlled_Buffer controlled_buffer_3
  assign controlled_buffer_1_out = in_1 ? {in_9, in_8, in_7, in_6, in_5, in_4, in_3, in_2} : 8'bz;  // Controlled_Buffer controlled_buffer_4
  Register RAM_Register (
    .D(controlled_buffer_1_out), .en(rom_1_data[5]), .Q(RAM_Register_q), .clk(clock_1_out));  // open: clr
  RAM #(.bus("separate")) ram_1 (
    .addr(RAM_Register_q), .din(controlled_buffer_1_out), .data(controlled_buffer_1_out),
    .str(rom_1_data[6]), .clk(clock_1_out), .ld(rom_1_data[7]));  // open: sel, clr
  assign controlled_buffer_1_out = rom_1_data[10] ? Program_Counter_q : 8'bz;  // Controlled_Buffer controlled_buffer_5
  Counter Program_Counter (
    .count(rom_1_data[9]), .Q(Program_Counter_q), .clk(clock_1_out));  // open: load, D, carry, clr
endmodule
