// Logisim project WolfCPU2.circ as structural Verilog: 3 circuits, main circuit main
module main (
  output [7:0] out_1
);

  wire ALU_Out, ALU_Sel, Carry, clock_1_out, Clock_A, Clock_B, Halt, IC_Reset, IR_In, IR_Param_Out, PC_Count,
       PC_Jump, RA_In, RA_Out, Ram_Addr_In, Ram_Out, Ram_Store, RB_In, RB_Out, RC_In, RC_Out, RD_In, RD_Out;
  wire [3:0] Instruction_Counter_q;
  wire [7:0] alu_1_out_4, counter_1_q, ram_1_data, register_1_q, register_1_q_2, register_2_q, register_3_q,
       register_4_q, register_5_q, register_6_q;
  wire [15:0] rom_1_data;

  Clock clock_1 (.out(clock_1_out));
  and and_1 (Clock_A, clock_1_out, ~Halt);  // AND_Gate
  Counter counter_1 (.load(PC_Jump), .D(out_1), .count(PC_Count), .Q(counter_1_q), .clk(Clock_A));  // open: carry, clr
  Counter #(.width(4), .max('hf)) Instruction_Counter (
    .Q(Instruction_Counter_q), .clk(Clock_B), .clr(IC_Reset));  // open: load, D, count, carry
  not not_1 (Clock_B, Clock_A);
  ROM #(.dataWidth(16)) rom_1 (.addr(counter_1_q), .data(rom_1_data));  // open: sel
  Control control_1 (
    .Instruction(register_1_q_2), .Instruction_Counter(Instruction_Counter_q), .Carry(Carry),
    .out_4(PC_Count), .out_5(PC_Jump), .out_6(IR_In), .out_7(IR_Param_Out), .out_8(RA_Out), .out_9(RA_In),
    .out_10(RB_Out), .out_11(RB_In), .out_12(RC_Out), .out_13(RC_In), .out_14(RD_Out), .out_15(RD_In),
    .out_16(ALU_Out), .out_17(ALU_Sel), .out_18(IC_Reset), .out_19(Halt), .out_20(Ram_Addr_In),
    .out_21(Ram_Store), .out_22(Ram_Out));
  Register #(.width(16)) register_1 (
    .D(rom_1_data), .en(IR_In), .Q({register_1_q_2, register_1_q}), .clk(Clock_A));  // open: clr
  assign out_1 = IR_Param_Out ? register_1_q : 8'bz;  // Controlled_Buffer controlled_buffer_1
  Register register_2 (.D(out_1), .en(Ram_Addr_In), .Q(register_2_q), .clk(Clock_A));  // open: clr
  Register register_3 (.D(out_1), .en(RA_In), .Q(register_3_q), .clk(Clock_A));  // open: clr
  assign out_1 = RA_Out ? register_3_q : 8'bz;  // Controlled_Buffer controlled_buffer_2
  assign out_1 = RB_Out ? register_4_q : 8'bz;  // Controlled_Buffer controlled_buffer_3
  Register register_4 (.D(out_1), .en(RB_In), .Q(register_4_q), .clk(Clock_A));  // open: clr
  assign out_1 = RC_Out ? register_5_q : 8'bz;  // Controlled_Buffer controlled_buffer_4
  Register register_5 (.D(out_1), .en(RC_In), .Q(register_5_q), .clk(Clock_A));  // open: clr
  Register register_6 (.D(out_1), .en(RD_In), .Q(register_6_q), .clk(Clock_A));  // open: clr
  assign out_1 = RD_Out ? register_6_q : 8'bz;  // Controlled_Buffer controlled_buffer_5
  ALU alu_1 (.Input_A(register_3_q), .Input_B(register_4_q), .out_4(alu_1_out_4), .in_1(ALU_Sel), .out_5(Carry));
  // Probe on register_4_q
  assign out_1 = Ram_Out ? ram_1_data : 8'bz;  // Controlled_Buffer controlled_buffer_6
  RAM #(.bus("separate")) ram_1 (
    .addr(register_2_q), .din(out_1), .data(ram_1_data), .str(Ram_Store), .clk(Clock_A));  // open: sel, ld, clr
  assign out_1 = ALU_Out ? alu_1_out_4 : 8'bz;  // Controlled_Buffer controlled_buffer_7

  // Other names for the same wires on the sheet: Main_Bus[7:0] = out_1

  // Notes on the sheet:
  //   contents of rom_1 (hex, n*v repeats v):
  //   1f00 1701 f01 300 1900 4300 f01 400 b00 1800 100 a00 1400 8803 5900 c000
endmodule

module ALU (
  input  in_1,
  input  [7:0] Input_A,
  input  [7:0] Input_B,
  output [7:0] out_4,
  output out_5
);

  wire adder_1_cout, and_1_out, and_2_out, not_1_out, not_2_out, subtractor_1_bout;
  wire [7:0] adder_1_out, subtractor_1_out;

  not not_1 (not_1_out, in_1);
  Adder adder_1 (.a(Input_A), .b(Input_B), .out(adder_1_out), .cout(adder_1_cout));  // open: cin
  assign out_4 = not_1_out ? adder_1_out : 8'bz;  // Controlled_Buffer controlled_buffer_1
  assign out_4 = in_1 ? subtractor_1_out : 8'bz;  // Controlled_Buffer controlled_buffer_2
  Subtractor subtractor_1 (.a(Input_A), .b(Input_B), .out(subtractor_1_out), .bout(subtractor_1_bout));  // open: bin
  and and_1 (and_1_out, subtractor_1_bout, in_1);
  not not_2 (not_2_out, in_1);
  and and_2 (and_2_out, adder_1_cout, not_2_out);
  or or_1 (out_5, and_1_out, and_2_out);
  // Probe on out_4

  // Other names for the same wires on the sheet: A[7:0] = Input_A; B[7:0] = Input_B
endmodule

module Control (
  input  [7:0] Instruction,
  input  [3:0] Instruction_Counter,
  input  Carry,
  output out_4,
  output out_5,
  output out_6,
  output out_7,
  output out_8,
  output out_9,
  output out_10,
  output out_11,
  output out_12,
  output out_13,
  output out_14,
  output out_15,
  output out_16,
  output out_17,
  output out_18,
  output out_19,
  output out_20,
  output out_21,
  output out_22
);

  wire [12:12] not_1_out;

  not not_1 (not_1_out[12], Carry);
  ROM #(.addrWidth(13), .dataWidth(19)) rom_1 (
    .addr({not_1_out[12], Instruction_Counter, Instruction}),
    .data({out_22, out_21, out_20, out_19, out_18, out_17, out_16, out_15, out_14, out_13, out_12, out_11, out_10, out_9, out_8, out_7, out_6, out_5, out_4}));  // open: sel

  // Other names for the same wires on the sheet: PC_Count = out_4; PC_Jump = out_5; IR_In = out_6;
  //   IR_Param_Out = out_7; RA_Out = out_8; RA_In = out_9; RB_Out = out_10; RB_In = out_11; RC_Out = out_12;
  //   RC_In = out_13; RD_Out = out_14; RD_In = out_15; ALU_Out = out_16; ALU_Sel = out_17; IC_Reset = out_18;
  //   Halt = out_19; Ram_Addr_In = out_20; Ram_Store = out_21; Ram_Out = out_22

  // Notes on the sheet:
  //   out_4: pull=down
  //   contents of rom_1 (hex, n*v repeats v):
  //   256*5 30 60 120 420 1020 3020 10008 28 90 c0 180 480 1080 3080 10008 88 210 240 300 600 1200 3200
  //   10008 208 810 840 900 c00 1800 3800 10008 808 10 50 110 410 1010 3010 10008 18 50 40 140 440 1040
  //   3040 10008 48 110 140 100 500 1100 3100 10008 108 410 440 500 400 1400 3400 10008 408 8*10010
  //   8*10040 8*10100 8*10400 8*11000 8*13000 8*50000 8*10008 8*a 56*4000 64*8000 6*4000 40020 7*4000
  //   40080 7*4000 40200 7*4000 40800 7*4000 40010 7*4000 40040 7*4000 40100 7*4000 40400 4000 20010 20040
  //   20100 20400 21000 23000 4000 20008 20010 20040 20100 20400 21000 23000 4000 20008 20010 20040 20100
  //   20400 21000 23000 4000 20008 20010 20040 20100 20400 21000 23000 4000 20008 20010 20040 20100 20400
  //   21000 23000 4000 20008 20010 20040 20100 20400 21000 23000 4000 20008 20010 20040 20100 20400 21000
  //   23000 4000 20008 20010 20040 20100 20400 21000 23000 4000 20008 64*4000 64*8000 192*4000 64*8000
  //   192*4000 64*8000 192*4000 64*8000 192*4000 64*8000 192*4000 64*8000 192*4000 64*8000 192*4000
  //   64*8000 192*4000 64*8000 192*4000 64*8000 192*4000 64*8000 192*4000 64*8000 192*4000 64*8000
  //   192*4000 64*8000 256*5 30 60 120 420 1020 3020 10008 28 90 c0 180 480 1080 3080 10008 88 210 240 300
  //   600 1200 3200 10008 208 810 840 900 c00 1800 3800 10008 808 10 50 110 410 1010 3010 10008 18 50 40
  //   140 440 1040 3040 10008 48 110 140 100 500 1100 3100 10008 108 410 440 500 400 1400 3400 10008 408
  //   8*10010 8*10040 8*10100 8*10400 8*11000 8*13000 8*50000 8*10008 16*a 48*4000 64*8000 6*4000 40020
  //   7*4000 40080 7*4000 40200 7*4000 40800 7*4000 40010 7*4000 40040 7*4000 40100 7*4000 40400 4000
  //   20010 20040 20100 20400 21000 23000 4000 20008 20010 20040 20100 20400 21000 23000 4000 20008 20010
  //   20040 20100 20400 21000 23000 4000 20008 20010 20040 20100 20400 21000 23000 4000 20008 20010 20040
  //   20100 20400 21000 23000 4000 20008 20010 20040 20100 20400 21000 23000 4000 20008 20010 20040 20100
  //   20400 21000 23000 4000 20008 20010 20040 20100 20400 21000 23000 4000 20008 64*4000 64*8000 192*4000
  //   64*8000 192*4000 64*8000 192*4000 64*8000 192*4000 64*8000 192*4000 64*8000 192*4000 64*8000
  //   192*4000 64*8000 192*4000 64*8000 192*4000 64*8000 192*4000 64*8000 192*4000 64*8000 192*4000
  //   64*8000 192*4000 64*8000
endmodule
