// Logisim project WolfCPU4.circ as structural Verilog
module main (
);

  wire CEnable, clock_1_out, Clock_A, Clock_B, decoder_1_out0, decoder_1_out1, decoder_1_out2,
       decoder_1_out3, Halt, Jump, Next_Instruction, not_1_out, not_2_out, not_3_out, or_1_out, RamWrite,
       RegWrite;
  wire [2:0] counter_1_q;
  wire [7:0] Program_Counter_q;
  wire [15:0] Addr, alu_1_out_4, Data, multiplexer_1_out, PC, Ramout, register_page_1_out_7;
  wire [31:0] Instruction;

  not not_1 (not_1_out, CEnable);
  Counter #(.width(3), .max('h7)) counter_1 (
    .count(not_1_out), .Q(counter_1_q), .clk(Clock_B), .clr(Next_Instruction));  // open: load, D, carry
  Decoder #(.select(3), .disabled(0), .enable("false")) decoder_1 (
    .out0(decoder_1_out0), .out1(decoder_1_out1), .out2(decoder_1_out2), .out3(decoder_1_out3),
    .out4(CEnable), .sel(counter_1_q));  // open: out5, out6, out7
  Counter Program_Counter (
    .count(CEnable), .Q(Program_Counter_q), .clk(Clock_B), .clr(not_2_out));  // open: load, D, carry
  not not_2 (not_2_out, CEnable);
  not not_3 (not_3_out, not_2_out);
  Register #(.width(16)) register_1 (
    .D(Ramout), .en(decoder_1_out0), .Q(Instruction[31:16]), .clk(Clock_A));  // open: clr
  Register #(.width(16)) register_2 (
    .D(Ramout), .en(decoder_1_out2), .Q(Instruction[15:0]), .clk(Clock_A));  // open: clr
  Control control_1 (
    .Opcode(Instruction[31:26]), .Step(Program_Counter_q), .Next_Instruction(Next_Instruction),
    .Ram_Store(RamWrite), .Register_Store(RegWrite), .Enable(not_3_out), .Halt(Halt), .Jump(Jump));
  or or_1 (or_1_out, decoder_1_out1, decoder_1_out3);
  Clock clock_1 (.out(clock_1_out));
  Counter #(.width(16), .max('hffff)) Program_Counter_2 (
    .load(Jump), .D(Data), .count(or_1_out), .Q(PC), .clk(Clock_A));  // open: carry, clr
  nor nor_1 (Clock_B, clock_1_out, Halt);
  not not_4 (Clock_A, Clock_B);
  Multiplexer #(.width(16), .enable("false")) multiplexer_1 (
    .in0(PC), .in1(Addr), .out(multiplexer_1_out), .sel(CEnable));
  Register_Page register_page_1 (
    .Read_Select_B(Instruction[20:16]), .Read_Select_A(Instruction[15:11]),
    .Write_Select(Instruction[25:21]), .Write_Data(Data), .Clock(Clock_A), .Write_Enable(RegWrite),
    .out_7(register_page_1_out_7), .out_8(Addr));
  Multiplexer #(.select(2), .width(16), .enable("false")) multiplexer_2 (
    .in0(alu_1_out_4), .in1(Instruction[15:0]), .in2(Ramout), .in3(register_page_1_out_7), .out(Data),
    .sel(Instruction[27:26]));
  RAM #(.addrWidth(16), .dataWidth(16), .bus("separate")) ram_1 (
    .addr(multiplexer_1_out), .din(Data), .data(Ramout), .str(RamWrite), .clk(Clock_A), .ld(1'b1));  // open: sel, clr
  ALU alu_1 (.in_1(Addr), .in_2(register_page_1_out_7), .out_4(alu_1_out_4), .in_3(Instruction[3:0]));

  // Other names for the same wires on the sheet: RASel = CEnable
endmodule

module ALU (
  input  [15:0] in_1,
  input  [15:0] in_2,
  input  [3:0] in_3,
  output [15:0] out_4
);

  wire [15:0] adder_1_out, and_1_out, comparator_1_eq, comparator_1_gt, comparator_1_lt, divider_1_out,
       multiplier_1_out, not_1_out, or_1_out, or_2_out, or_3_out, shifter_1_out, shifter_2_out,
       shifter_3_out, subtractor_1_out, xor_1_out;

  Adder #(.width(16)) adder_1 (.a(in_1), .b(in_2), .out(adder_1_out));  // open: cin, cout
  Subtractor #(.width(16)) subtractor_1 (.a(in_1), .b(in_2), .out(subtractor_1_out));  // open: bin, bout
  Multiplier #(.width(16)) multiplier_1 (.a(in_1), .b(in_2), .out(multiplier_1_out));  // open: cin, cout
  Divider #(.width(16)) divider_1 (.a(in_1), .b(in_2), .out(divider_1_out));  // open: upper, rem
  Shifter #(.width(16)) shifter_1 (.in(in_1), .\dist (in_2[3:0]), .out(shifter_1_out));
  Shifter #(.width(16), .shift("lr")) shifter_2 (.in(in_1), .\dist (in_2[3:0]), .out(shifter_2_out));
  Shifter #(.width(16), .shift("ar")) shifter_3 (.in(in_1), .\dist (in_2[3:0]), .out(shifter_3_out));
  assign and_1_out = in_1 & in_2;  // AND_Gate and_1, 16 bits wide
  assign or_1_out = in_1 | in_2;  // OR_Gate or_1, 16 bits wide
  assign xor_1_out = in_1 ^ in_2;  // XOR_Gate xor_1, 16 bits wide
  assign not_1_out = ~in_1;  // NOT_Gate not_1, 16 bits wide
  Comparator #(.width(16)) comparator_1 (
    .a(in_1), .b(in_2), .gt(comparator_1_gt[0]), .eq(comparator_1_eq[0]), .lt(comparator_1_lt[0]));
  or or_2 (or_2_out[0], comparator_1_gt[0], comparator_1_eq[0]);
  or or_3 (or_3_out[0], comparator_1_eq[0], comparator_1_lt[0]);
  Pull_Resistor pull_resistor_1 (.node(or_3_out));
  Pull_Resistor pull_resistor_2 (.node(comparator_1_lt));
  Multiplexer #(.select(4), .width(16), .enable("false")) multiplexer_1 (
    .in0(adder_1_out), .in1(subtractor_1_out), .in2(multiplier_1_out), .in3(divider_1_out),
    .in4(shifter_1_out), .in5(shifter_2_out), .in6(shifter_3_out), .in7(and_1_out), .in8(or_1_out),
    .in9(xor_1_out), .in10(not_1_out), .in11(comparator_1_lt), .in12(or_3_out), .in13(comparator_1_eq),
    .in14(or_2_out), .in15(comparator_1_gt), .out(out_4), .sel(in_3));
  Pull_Resistor pull_resistor_3 (.node(comparator_1_gt));
  Pull_Resistor pull_resistor_4 (.node(or_2_out));
  Pull_Resistor pull_resistor_5 (.node(comparator_1_eq));
endmodule

module Register_Page (
  input  Write_Enable,
  input  [4:0] Read_Select_B,
  input  [4:0] Read_Select_A,
  input  [4:0] Write_Select,
  input  [15:0] Write_Data,
  input  Clock,
  output [15:0] out_7,
  output [15:0] out_8
);

  wire demultiplexer_1_out0, demultiplexer_1_out1, demultiplexer_1_out2, demultiplexer_1_out3,
       demultiplexer_1_out4, demultiplexer_1_out5, demultiplexer_1_out6, demultiplexer_1_out7,
       demultiplexer_2_out0, demultiplexer_2_out1, demultiplexer_2_out2, demultiplexer_2_out3,
       demultiplexer_3_out0, demultiplexer_3_out1, demultiplexer_3_out2, demultiplexer_3_out3,
       demultiplexer_3_out4, demultiplexer_3_out5, demultiplexer_3_out6, demultiplexer_3_out7,
       demultiplexer_4_out0, demultiplexer_4_out1, demultiplexer_4_out2, demultiplexer_4_out3,
       demultiplexer_4_out4, demultiplexer_4_out5, demultiplexer_4_out6, demultiplexer_4_out7,
       demultiplexer_5_out0, demultiplexer_5_out1, demultiplexer_5_out2, demultiplexer_5_out3,
       demultiplexer_5_out4, demultiplexer_5_out5, demultiplexer_5_out6, demultiplexer_5_out7;
  wire [15:0] multiplexer_2_out, multiplexer_4_out, multiplexer_5_out, multiplexer_6_out, multiplexer_7_out,
       multiplexer_8_out, multiplexer_9_out, multiplexer_10_out, register_1_q, register_2_q, register_3_q,
       register_4_q, register_5_q, register_6_q, register_7_q, register_8_q, register_9_q, register_10_q,
       register_11_q, register_12_q, register_13_q, register_14_q, register_15_q, register_16_q,
       register_17_q, register_18_q, register_19_q, register_20_q, register_21_q, register_22_q,
       register_23_q, register_24_q, register_25_q, register_26_q, register_27_q, register_28_q,
       register_29_q, register_30_q, register_31_q, register_32_q;

  Demultiplexer #(.select(3), .enable("false")) demultiplexer_1 (
    .out0(demultiplexer_1_out0), .out1(demultiplexer_1_out1), .out2(demultiplexer_1_out2),
    .out3(demultiplexer_1_out3), .out4(demultiplexer_1_out4), .out5(demultiplexer_1_out5),
    .out6(demultiplexer_1_out6), .out7(demultiplexer_1_out7), .in(demultiplexer_2_out0),
    .sel(Write_Select[2:0]));
  Demultiplexer #(.select(2), .enable("false")) demultiplexer_2 (
    .out0(demultiplexer_2_out0), .out1(demultiplexer_2_out1), .out2(demultiplexer_2_out2),
    .out3(demultiplexer_2_out3), .in(Write_Enable), .sel(Write_Select[4:3]));
  Multiplexer #(.select(2), .width(16), .enable("false")) multiplexer_1 (
    .in0(multiplexer_2_out), .in1(multiplexer_5_out), .in2(multiplexer_7_out), .in3(multiplexer_9_out),
    .out(out_7), .sel(Read_Select_A[4:3]));
  Multiplexer #(.select(3), .width(16), .enable("false")) multiplexer_2 (
    .in0(register_1_q), .in1(register_2_q), .in2(register_3_q), .in3(register_4_q), .in4(register_5_q),
    .in5(register_6_q), .in6(register_7_q), .in7(register_8_q), .out(multiplexer_2_out),
    .sel(Read_Select_A[2:0]));
  Register #(.width(16)) register_1 (
    .D(Write_Data), .en(demultiplexer_1_out0), .Q(register_1_q), .clk(Clock));  // open: clr
  Register #(.width(16)) register_2 (
    .D(Write_Data), .en(demultiplexer_1_out1), .Q(register_2_q), .clk(Clock));  // open: clr
  Register #(.width(16)) register_3 (
    .D(Write_Data), .en(demultiplexer_1_out2), .Q(register_3_q), .clk(Clock));  // open: clr
  Register #(.width(16)) register_4 (
    .D(Write_Data), .en(demultiplexer_1_out3), .Q(register_4_q), .clk(Clock));  // open: clr
  Register #(.width(16)) register_5 (
    .D(Write_Data), .en(demultiplexer_1_out4), .Q(register_5_q), .clk(Clock));  // open: clr
  Register #(.width(16)) register_6 (
    .D(Write_Data), .en(demultiplexer_1_out5), .Q(register_6_q), .clk(Clock));  // open: clr
  Register #(.width(16)) register_7 (
    .D(Write_Data), .en(demultiplexer_1_out6), .Q(register_7_q), .clk(Clock));  // open: clr
  Register #(.width(16)) register_8 (
    .D(Write_Data), .en(demultiplexer_1_out7), .Q(register_8_q), .clk(Clock));  // open: clr
  Multiplexer #(.select(2), .width(16), .enable("false")) multiplexer_3 (
    .in0(multiplexer_4_out), .in1(multiplexer_6_out), .in2(multiplexer_8_out), .in3(multiplexer_10_out),
    .out(out_8), .sel(Read_Select_B[4:3]));
  Multiplexer #(.select(3), .width(16), .enable("false")) multiplexer_4 (
    .in0(register_1_q), .in1(register_2_q), .in2(register_3_q), .in3(register_4_q), .in4(register_5_q),
    .in5(register_6_q), .in6(register_7_q), .in7(register_8_q), .out(multiplexer_4_out),
    .sel(Read_Select_B[2:0]));
  Demultiplexer #(.select(3), .enable("false")) demultiplexer_3 (
    .out0(demultiplexer_3_out0), .out1(demultiplexer_3_out1), .out2(demultiplexer_3_out2),
    .out3(demultiplexer_3_out3), .out4(demultiplexer_3_out4), .out5(demultiplexer_3_out5),
    .out6(demultiplexer_3_out6), .out7(demultiplexer_3_out7), .in(demultiplexer_2_out1),
    .sel(Write_Select[2:0]));
  Multiplexer #(.select(3), .width(16), .enable("false")) multiplexer_5 (
    .in0(register_9_q), .in1(register_10_q), .in2(register_11_q), .in3(register_12_q), .in4(register_13_q),
    .in5(register_14_q), .in6(register_15_q), .in7(register_16_q), .out(multiplexer_5_out),
    .sel(Read_Select_A[2:0]));
  Register #(.width(16)) register_9 (
    .D(Write_Data), .en(demultiplexer_3_out0), .Q(register_9_q), .clk(Clock));  // open: clr
  Register #(.width(16)) register_10 (
    .D(Write_Data), .en(demultiplexer_3_out1), .Q(register_10_q), .clk(Clock));  // open: clr
  Register #(.width(16)) register_11 (
    .D(Write_Data), .en(demultiplexer_3_out2), .Q(register_11_q), .clk(Clock));  // open: clr
  Register #(.width(16)) register_12 (
    .D(Write_Data), .en(demultiplexer_3_out3), .Q(register_12_q), .clk(Clock));  // open: clr
  Register #(.width(16)) register_13 (
    .D(Write_Data), .en(demultiplexer_3_out4), .Q(register_13_q), .clk(Clock));  // open: clr
  Register #(.width(16)) register_14 (
    .D(Write_Data), .en(demultiplexer_3_out5), .Q(register_14_q), .clk(Clock));  // open: clr
  Register #(.width(16)) register_15 (
    .D(Write_Data), .en(demultiplexer_3_out6), .Q(register_15_q), .clk(Clock));  // open: clr
  Register #(.width(16)) register_16 (
    .D(Write_Data), .en(demultiplexer_3_out7), .Q(register_16_q), .clk(Clock));  // open: clr
  Multiplexer #(.select(3), .width(16), .enable("false")) multiplexer_6 (
    .in0(register_9_q), .in1(register_10_q), .in2(register_11_q), .in3(register_12_q), .in4(register_13_q),
    .in5(register_14_q), .in6(register_15_q), .in7(register_16_q), .out(multiplexer_6_out),
    .sel(Read_Select_B[2:0]));
  Demultiplexer #(.select(3), .enable("false")) demultiplexer_4 (
    .out0(demultiplexer_4_out0), .out1(demultiplexer_4_out1), .out2(demultiplexer_4_out2),
    .out3(demultiplexer_4_out3), .out4(demultiplexer_4_out4), .out5(demultiplexer_4_out5),
    .out6(demultiplexer_4_out6), .out7(demultiplexer_4_out7), .in(demultiplexer_2_out2),
    .sel(Write_Select[2:0]));
  Register #(.width(16)) register_17 (
    .D(Write_Data), .en(demultiplexer_4_out0), .Q(register_17_q), .clk(Clock));  // open: clr
  Register #(.width(16)) register_18 (
    .D(Write_Data), .en(demultiplexer_4_out1), .Q(register_18_q), .clk(Clock));  // open: clr
  Register #(.width(16)) register_19 (
    .D(Write_Data), .en(demultiplexer_4_out2), .Q(register_19_q), .clk(Clock));  // open: clr
  Register #(.width(16)) register_20 (
    .D(Write_Data), .en(demultiplexer_4_out3), .Q(register_20_q), .clk(Clock));  // open: clr
  Register #(.width(16)) register_21 (
    .D(Write_Data), .en(demultiplexer_4_out4), .Q(register_21_q), .clk(Clock));  // open: clr
  Register #(.width(16)) register_22 (
    .D(Write_Data), .en(demultiplexer_4_out5), .Q(register_22_q), .clk(Clock));  // open: clr
  Register #(.width(16)) register_23 (
    .D(Write_Data), .en(demultiplexer_4_out6), .Q(register_23_q), .clk(Clock));  // open: clr
  Register #(.width(16)) register_24 (
    .D(Write_Data), .en(demultiplexer_4_out7), .Q(register_24_q), .clk(Clock));  // open: clr
  Multiplexer #(.select(3), .width(16), .enable("false")) multiplexer_7 (
    .in0(register_17_q), .in1(register_18_q), .in2(register_19_q), .in3(register_20_q), .in4(register_21_q),
    .in5(register_22_q), .in6(register_23_q), .in7(register_24_q), .out(multiplexer_7_out),
    .sel(Read_Select_A[2:0]));
  Multiplexer #(.select(3), .width(16), .enable("false")) multiplexer_8 (
    .in0(register_17_q), .in1(register_18_q), .in2(register_19_q), .in3(register_20_q), .in4(register_21_q),
    .in5(register_22_q), .in6(register_23_q), .in7(register_24_q), .out(multiplexer_8_out),
    .sel(Read_Select_B[2:0]));
  Demultiplexer #(.select(3), .enable("false")) demultiplexer_5 (
    .out0(demultiplexer_5_out0), .out1(demultiplexer_5_out1), .out2(demultiplexer_5_out2),
    .out3(demultiplexer_5_out3), .out4(demultiplexer_5_out4), .out5(demultiplexer_5_out5),
    .out6(demultiplexer_5_out6), .out7(demultiplexer_5_out7), .in(demultiplexer_2_out3),
    .sel(Write_Select[2:0]));
  Register #(.width(16)) register_25 (
    .D(Write_Data), .en(demultiplexer_5_out0), .Q(register_25_q), .clk(Clock));  // open: clr
  Register #(.width(16)) register_26 (
    .D(Write_Data), .en(demultiplexer_5_out1), .Q(register_26_q), .clk(Clock));  // open: clr
  Register #(.width(16)) register_27 (
    .D(Write_Data), .en(demultiplexer_5_out2), .Q(register_27_q), .clk(Clock));  // open: clr
  Register #(.width(16)) register_28 (
    .D(Write_Data), .en(demultiplexer_5_out3), .Q(register_28_q), .clk(Clock));  // open: clr
  Register #(.width(16)) register_29 (
    .D(Write_Data), .en(demultiplexer_5_out4), .Q(register_29_q), .clk(Clock));  // open: clr
  Register #(.width(16)) register_30 (
    .D(Write_Data), .en(demultiplexer_5_out5), .Q(register_30_q), .clk(Clock));  // open: clr
  Register #(.width(16)) register_31 (
    .D(Write_Data), .en(demultiplexer_5_out6), .Q(register_31_q), .clk(Clock));  // open: clr
  Register #(.width(16)) register_32 (
    .D(Write_Data), .en(demultiplexer_5_out7), .Q(register_32_q), .clk(Clock));  // open: clr
  Multiplexer #(.select(3), .width(16), .enable("false")) multiplexer_9 (
    .in0(register_25_q), .in1(register_26_q), .in2(register_27_q), .in3(register_28_q), .in4(register_29_q),
    .in5(register_30_q), .in6(register_31_q), .in7(register_32_q), .out(multiplexer_9_out),
    .sel(Read_Select_A[2:0]));
  Multiplexer #(.select(3), .width(16), .enable("false")) multiplexer_10 (
    .in0(register_25_q), .in1(register_26_q), .in2(register_27_q), .in3(register_28_q), .in4(register_29_q),
    .in5(register_30_q), .in6(register_31_q), .in7(register_32_q), .out(multiplexer_10_out),
    .sel(Read_Select_B[2:0]));
endmodule

module Control (
  input  Enable,
  input  [5:0] Opcode,
  input  [7:0] Step,
  output Next_Instruction,
  output Ram_Store,
  output Register_Store,
  output Halt,
  output Jump
);

  wire [1:0] Jump_t, Store;
  wire [2:0] ALU, Load;

  Decoder #(.enable("false")) decoder_1 (.out0(ALU[2]), .out1(ALU[0]), .sel(Step[0]));
  Decoder #(.enable("false")) decoder_2 (.out0(Load[2]), .out1(Load[0]), .sel(Step[0]));
  Decoder #(.enable("false")) decoder_3 (.out0(Store[1]), .out1(Store[0]), .sel(Step[0]));
  Decoder #(.enable("false")) decoder_4 (.out0(Jump_t[1]), .out1(Jump_t[0]), .sel(Step[0]));
  Multiplexer #(.select(2), .width(3), .disabled(0)) multiplexer_1 (
    .in0({ALU[2], 1'b0, ALU[0]}), .in1({1'b0, Store}), .in2({Load[2], 1'b0, Load[0]}), .in3({1'b0, Jump_t}),
    .out({Register_Store, Ram_Store, Next_Instruction}), .sel(Opcode[5:4]), .en(Enable));

  assign Halt = 1'b0;
  assign Jump = 1'b0;

  // Other names for the same wires on the sheet: Instruction[5:0] = Opcode

  // Notes on the sheet:
  //   Next_Instruction: pull=down
  //   Ram_Store: pull=down
  //   Register_Store: pull=down
  //   Jump: pull=down
  //   Halt: pull=down
endmodule
