// Logisim project WolfCPU5.circ as structural Verilog: 1 circuit, main circuit main
module main (
  input  Clock_Enable,
  input  in_2,
  input  in_3,
  input  in_4,
  input  in_5,
  input  in_6,
  input  in_7,
  input  in_8,
  input  in_9,
  input  in_10,
  input  in_11,
  input  in_12,
  input  in_13,
  input  in_14,
  input  in_15,
  input  in_16,
  input  in_17,
  input  in_18,
  input  in_19,
  input  in_20,
  input  in_21,
  input  in_22
);

  wire _Clk, and_1_out, Clk, clock_1_out, Left_Op_LSB_Store, Left_Op_MSB_Store, LSB_2_carry,
       Right_Op_LSB_Store, Right_Op_RSB_Store, Step_out;
  wire [7:0] A_q, B_q, C_q, D_q, Instruction_Register_q, L_LSB_q, L_MSB_q, LSB_2_q, LSB_q, Main_Bus, MSB_2_q,
       MSB_q, R_LSB_q, R_MSBD_q;
  wire [15:0] adder_1_out;

  Clock clock_1 (.out(clock_1_out));
  Button Step (.out(Step_out));
  Register A (.D(Main_Bus), .en(in_10), .Q(A_q), .clk(Clk));  // open: clr
  assign Main_Bus = in_11 ? A_q : 8'bz;  // Controlled_Buffer controlled_buffer_1
  and and_1 (and_1_out, Clock_Enable, clock_1_out);
  or or_1 (Clk, and_1_out, Step_out);
  Register B (.D(Main_Bus), .en(in_13), .Q(B_q), .clk(Clk));  // open: clr
  not not_1 (_Clk, Clk);
  Register LSB (.D(Main_Bus), .en(in_5), .Q(LSB_q), .clk(Clk));  // open: clr
  assign Main_Bus = in_14 ? B_q : 8'bz;  // Controlled_Buffer controlled_buffer_2
  Register C (.D(Main_Bus), .en(in_16), .Q(C_q), .clk(Clk));  // open: clr
  Register L_MSB (.D(Main_Bus), .en(Left_Op_MSB_Store), .Q(L_MSB_q), .clk(Clk));  // open: clr
  Register R_LSB (.D(Main_Bus), .en(Right_Op_LSB_Store), .Q(R_LSB_q), .clk(Clk));  // open: clr
  Register MSB (.D(Main_Bus), .en(in_4), .Q(MSB_q), .clk(Clk));  // open: clr
  assign Main_Bus = in_17 ? C_q : 8'bz;  // Controlled_Buffer controlled_buffer_3
  Register D (.D(Main_Bus), .en(in_19), .Q(D_q), .clk(Clk));  // open: clr
  Register L_LSB (.D(Main_Bus), .en(Left_Op_LSB_Store), .Q(L_LSB_q), .clk(Clk));  // open: clr
  Register R_MSBD (.D(Main_Bus), .en(Right_Op_RSB_Store), .Q(R_MSBD_q), .clk(Clk));  // open: clr
  assign Main_Bus = in_20 ? D_q : 8'bz;  // Controlled_Buffer controlled_buffer_4
  assign Main_Bus = in_8 ? adder_1_out[7:0] : 8'bz;  // Controlled_Buffer controlled_buffer_5
  Adder #(.width(16)) adder_1 (.a({L_MSB_q, L_LSB_q}), .b({R_MSBD_q, R_LSB_q}), .out(adder_1_out));  // open: cin, cout
  assign Main_Bus = in_9 ? adder_1_out[15:8] : 8'bz;  // Controlled_Buffer controlled_buffer_6
  // Probe on Main_Bus
  RAM #(.addrWidth(16), .bus("separate")) ram_1 (
    .addr({MSB_q, LSB_q}), .din(Main_Bus), .data(Main_Bus), .str(in_6), .clk(Clk), .ld(in_7));  // open: sel, clr
  Register Instruction_Register (.D(Main_Bus), .en(in_2), .Q(Instruction_Register_q), .clk(Clk));  // open: clr
  Counter LSB_2 (.load(in_18), .D(Main_Bus), .count(in_12), .Q(LSB_2_q), .carry(LSB_2_carry), .clk(Clk));  // open: clr
  Counter MSB_2 (.load(in_15), .D(Main_Bus), .count(LSB_2_carry), .Q(MSB_2_q), .clk(Clk));  // open: carry, clr
  assign Main_Bus = in_3 ? Instruction_Register_q : 8'bz;  // Controlled_Buffer controlled_buffer_7
  assign Main_Bus = in_22 ? LSB_2_q : 8'bz;  // Controlled_Buffer controlled_buffer_8
  assign Main_Bus = in_21 ? MSB_2_q : 8'bz;  // Controlled_Buffer controlled_buffer_9

  // Other names for the same wires on the sheet: A_Load = in_11; A_Store = in_10; APU_LSB_Load = in_8;
  //   APU_MSB_Load = in_9; B_Load = in_14; B_Store = in_13; C_Load = in_17; C_Store = in_16; D_Load = in_20;
  //   D_Store = in_19; Instruction_Load = in_3; Instruction_Store = in_2; Memory_Load = in_7;
  //   Memory_LSB_Enable = in_5; Memory_MSB_Enable = in_4; Memory_Store = in_6; Prog_Count_Enable = in_12;
  //   Prog_LSB_Load = in_22; Prog_LSB_Store = in_18; Prog_MSB_Load = in_21; Prog_MSB_Store = in_15
endmodule
