// Logisim project WolfPU.circ as structural Verilog: 4 circuits, main circuit main
module main (
);

  wire Acl_Reg_A, Acl_Reg_B, clock_1_out, Clock_A, Clock_B, Halt, IR_En, Jump, Jump_Addr_Sel, Output_Sel,
       PC_Enable, PR_En, RAM_Addr_Sel, RegInSel, Register_EN;
  wire [7:0] alu_1_out_4, multiplexer_3_out, multiplexer_4_out, ram_1_data, register_1_q, register_2_q,
       register_3_q, register_4_q, register_page_1_out_a, register_page_1_out_b;
  wire [15:0] adder_1_out, bit_extender_1_out, counter_1_q, multiplexer_1_out, multiplexer_2_out;

  Register register_1 (.D(multiplexer_4_out), .en(Acl_Reg_A), .Q(register_1_q), .clk(Clock_A));  // open: clr
  Register register_2 (.D(multiplexer_4_out), .en(Acl_Reg_B), .Q(register_2_q), .clk(Clock_A));  // open: clr
  assign bit_extender_1_out = {{8{multiplexer_4_out[7]}}, multiplexer_4_out};  // Bit_Extender bit_extender_1
  Adder #(.width(16)) adder_1 (
    .a({register_2_q, register_1_q}), .b(bit_extender_1_out), .out(adder_1_out));  // open: cin, cout
  Multiplexer #(.width(16), .disabled(0), .enable("false")) multiplexer_1 (
    .in0({register_2_q, register_1_q}), .in1(adder_1_out), .out(multiplexer_1_out), .sel(Jump_Addr_Sel));
  Counter #(.width(16), .max('hffff)) counter_1 (
    .load(Jump), .D(multiplexer_1_out), .count(PC_Enable), .Q(counter_1_q), .clk(Clock_A));  // open: carry, clr
  Control control_1 (
    .Register_EN(Register_EN), .Output_Sel(Output_Sel), .Reg_In_Sel(RegInSel), .PR_En(PR_En), .IR_En(IR_En),
    .PC_En(PC_Enable), .Jump_Addr_Sel(Jump_Addr_Sel), .Ram_Addr_Sel(RAM_Addr_Sel), .Acl_Reg_A(Acl_Reg_A),
    .ACL_Reg_B(Acl_Reg_B), .Halt(Halt), .Operation(register_3_q[7:4]), .Clock(Clock_B), .Jump(Jump));
  Clock clock_1 (.out(clock_1_out));
  Multiplexer #(.width(16), .enable("false")) multiplexer_2 (
    .in0(multiplexer_1_out), .in1(counter_1_q), .out(multiplexer_2_out), .sel(RAM_Addr_Sel));
  and and_1 (Clock_A, clock_1_out, ~Halt);  // AND_Gate
  not not_1 (Clock_B, Clock_A);
  RAM #(.addrWidth(16), .bus("separate")) ram_1 (
    .addr(multiplexer_2_out), .din(multiplexer_4_out), .data(ram_1_data), .str(1'b0), .clk(Clock_A));  // open: sel, ld, clr
  Register register_3 (.D(ram_1_data), .en(IR_En), .Q(register_3_q), .clk(Clock_A));  // open: clr
  Register register_4 (.D(ram_1_data), .en(PR_En), .Q(register_4_q), .clk(Clock_A));  // open: clr
  Multiplexer #(.width(8), .enable("false")) multiplexer_3 (
    .in0(ram_1_data), .in1(multiplexer_4_out), .out(multiplexer_3_out), .sel(RegInSel));
  Register_Page register_page_1 (
    .W_Addr(register_4_q[3:0]), .Addr_A(register_4_q[3:0]), .Addr_B(register_4_q[7:4]),
    .W_Data(multiplexer_3_out), .Clock(Clock_A), .Write_En(Register_EN), .Out_A(register_page_1_out_a),
    .Out_B(register_page_1_out_b));
  ALU alu_1 (
    .Op_A(register_page_1_out_b), .Op_B(register_page_1_out_a), .out_4(alu_1_out_4),
    .Function(register_3_q[3:0]));  // open: out_5
  Multiplexer #(.width(8), .enable("false")) multiplexer_4 (
    .in0(register_page_1_out_b), .in1(alu_1_out_4), .out(multiplexer_4_out), .sel(Output_Sel));
endmodule

module ALU (
  input  [3:0] Function,
  input  [7:0] Op_A,
  input  [7:0] Op_B,
  output [7:0] out_4,
  output out_5
);

  Adder adder_1 (.a(Op_A), .b(Op_B), .out(out_4), .cout(out_5));  // open: cin
endmodule

module Register_Page (
  input  Write_En,
  input  [3:0] W_Addr,
  input  [3:0] Addr_A,
  input  [3:0] Addr_B,
  input  [7:0] W_Data,
  input  Clock,
  output [7:0] Out_A,
  output [7:0] Out_B
);

  wire demultiplexer_1_out0, demultiplexer_1_out1, demultiplexer_1_out2, demultiplexer_1_out3,
       demultiplexer_1_out4, demultiplexer_1_out5, demultiplexer_1_out6, demultiplexer_1_out7,
       demultiplexer_1_out8, demultiplexer_1_out9, demultiplexer_1_out10, demultiplexer_1_out11,
       demultiplexer_1_out12, demultiplexer_1_out13, demultiplexer_1_out14, demultiplexer_1_out15;
  wire [7:0] register_1_q, register_2_q, register_3_q, register_4_q, register_5_q, register_6_q,
       register_7_q, register_8_q, register_9_q, register_10_q, register_11_q, register_12_q, register_13_q,
       register_14_q, register_15_q, register_16_q;

  Demultiplexer #(.select(4), .disabled(0), .enable("false")) demultiplexer_1 (
    .out0(demultiplexer_1_out0), .out1(demultiplexer_1_out1), .out2(demultiplexer_1_out2),
    .out3(demultiplexer_1_out3), .out4(demultiplexer_1_out4), .out5(demultiplexer_1_out5),
    .out6(demultiplexer_1_out6), .out7(demultiplexer_1_out7), .out8(demultiplexer_1_out8),
    .out9(demultiplexer_1_out9), .out10(demultiplexer_1_out10), .out11(demultiplexer_1_out11),
    .out12(demultiplexer_1_out12), .out13(demultiplexer_1_out13), .out14(demultiplexer_1_out14),
    .out15(demultiplexer_1_out15), .in(Write_En), .sel(W_Addr));
  Register register_1 (.D(W_Data), .en(demultiplexer_1_out15), .Q(register_1_q), .clk(Clock));  // open: clr
  Register register_2 (.D(W_Data), .en(demultiplexer_1_out14), .Q(register_2_q), .clk(Clock));  // open: clr
  Register register_3 (.D(W_Data), .en(demultiplexer_1_out13), .Q(register_3_q), .clk(Clock));  // open: clr
  Register register_4 (.D(W_Data), .en(demultiplexer_1_out12), .Q(register_4_q), .clk(Clock));  // open: clr
  Register register_5 (.D(W_Data), .en(demultiplexer_1_out11), .Q(register_5_q), .clk(Clock));  // open: clr
  Register register_6 (.D(W_Data), .en(demultiplexer_1_out10), .Q(register_6_q), .clk(Clock));  // open: clr
  Register register_7 (.D(W_Data), .en(demultiplexer_1_out9), .Q(register_7_q), .clk(Clock));  // open: clr
  Register register_8 (.D(W_Data), .en(demultiplexer_1_out8), .Q(register_8_q), .clk(Clock));  // open: clr
  Register register_9 (.D(W_Data), .en(demultiplexer_1_out7), .Q(register_9_q), .clk(Clock));  // open: clr
  Register register_10 (.D(W_Data), .en(demultiplexer_1_out6), .Q(register_10_q), .clk(Clock));  // open: clr
  Register register_11 (.D(W_Data), .en(demultiplexer_1_out5), .Q(register_11_q), .clk(Clock));  // open: clr
  Register register_12 (.D(W_Data), .en(demultiplexer_1_out4), .Q(register_12_q), .clk(Clock));  // open: clr
  Register register_13 (.D(W_Data), .en(demultiplexer_1_out3), .Q(register_13_q), .clk(Clock));  // open: clr
  Register register_14 (.D(W_Data), .en(demultiplexer_1_out2), .Q(register_14_q), .clk(Clock));  // open: clr
  Register register_15 (.D(W_Data), .en(demultiplexer_1_out1), .Q(register_15_q), .clk(Clock));  // open: clr
  Register register_16 (.D(W_Data), .en(demultiplexer_1_out0), .Q(register_16_q), .clk(Clock));  // open: clr
  Multiplexer #(.select(4), .width(8), .enable("false")) multiplexer_1 (
    .in0(register_16_q), .in1(register_15_q), .in2(register_14_q), .in3(register_13_q), .in4(register_12_q),
    .in5(register_11_q), .in6(register_10_q), .in7(register_9_q), .in8(register_8_q), .in9(register_7_q),
    .in10(register_6_q), .in11(register_5_q), .in12(register_4_q), .in13(register_3_q), .in14(register_2_q),
    .in15(register_1_q), .out(Out_A), .sel(Addr_A));
  Multiplexer #(.select(4), .width(8), .enable("false")) multiplexer_2 (
    .in0(register_16_q), .in1(register_15_q), .in2(register_14_q), .in3(register_13_q), .in4(register_12_q),
    .in5(register_11_q), .in6(register_10_q), .in7(register_9_q), .in8(register_8_q), .in9(register_7_q),
    .in10(register_6_q), .in11(register_5_q), .in12(register_4_q), .in13(register_3_q), .in14(register_2_q),
    .in15(register_1_q), .out(Out_B), .sel(Addr_B));
endmodule

module Control (
  input  [3:0] Operation,
  input  Clock,
  output Register_EN,
  output Output_Sel,
  output Reg_In_Sel,
  output PR_En,
  output IR_En,
  output PC_En,
  output Jump_Addr_Sel,
  output Ram_Addr_Sel,
  output Acl_Reg_A,
  output ACL_Reg_B,
  output Halt,
  output Jump
);

  wire decoder_1_out0, decoder_1_out4, decoder_1_out5, decoder_1_out6, decoder_1_out7;
  wire [2:0] multiplexer_1_out, multiplexer_2_out, register_1_q;

  Multiplexer #(.select(4), .width(3), .enable("false")) multiplexer_1 (
    .in0(3'b001), .in8(3'b010), .out(multiplexer_1_out), .sel(Operation));  // open: in1, in2, in3, in4, in5, in6, in7, in9, in10, in11, in12, in13, in14, in15
  Multiplexer #(.select(3), .width(3)) multiplexer_2 (
    .in0(3'b001), .in1(multiplexer_1_out), .in2(3'b011), .in3(3'b001), .out(multiplexer_2_out),
    .sel(register_1_q));  // open: in4, in5, in6, in7, en
  Register #(.width(3)) register_1 (.D(multiplexer_2_out), .Q(register_1_q), .clk(Clock));  // open: en, clr
  Decoder #(.select(3), .disabled(0), .enable("false")) decoder_1 (
    .out0(decoder_1_out0), .out1(IR_En), .out2(PR_En), .out3(Output_Sel), .out4(decoder_1_out4),
    .out5(decoder_1_out5), .out6(decoder_1_out6), .out7(decoder_1_out7), .sel(register_1_q));
  or or_1 (PC_En, IR_En, PR_En);

  assign Acl_Reg_A = 1'b0;
  assign ACL_Reg_B = 1'b0;
  assign Halt = 1'b0;
  assign Jump = 1'b0;
  assign Jump_Addr_Sel = 1'b0;
  assign Ram_Addr_Sel = 1'b0;
  assign Reg_In_Sel = Output_Sel;
  assign Register_EN = Output_Sel;
endmodule
