// Logisim project WolfAVR.circ as structural Verilog: 5 circuits, main circuit main
module main (
);

  wire alu_1__2s_overflow_out, alu_1_carry_out, alu_1_negative_out, alu_1_zero_out, ALU_En, C, Cen, Clock,
       IR_En, N, Nen, not_1_out, PC_En, PC_Load, Ram_Load, Ram_Store, Reg_In_Sel, Reg_WEn, V, Ven, Z, Zen;
  wire [2:0] Addr_Sel;
  wire [4:0] multiplexer_1_out, register_1_q, register_1_q_2;
  wire [7:0] alu_1_result, register_page_1_data_a, register_page_1_data_b;
  wire [15:0] counter_1_q, multiplexer_2_out, register_page_1_x, register_page_1_y, register_page_1_z,
       rom_1_data, undriven;
  wire [15:10] register_1_q_3;

  Clock clock_1 (.out(Clock));
  Counter #(.width(16), .max('hffff)) counter_1 (
    .load(PC_Load), .D(multiplexer_2_out), .count(PC_En), .Q(counter_1_q), .clk(Clock));  // open: carry, clr
  Multiplexer #(.width(5), .enable("false")) multiplexer_1 (
    .in0(register_1_q_2), .in1(register_1_q), .out(multiplexer_1_out), .sel(Reg_In_Sel));
  ROM #(.addrWidth(16), .dataWidth(16)) rom_1 (.addr(counter_1_q), .data(rom_1_data));  // open: sel
  Register_Page register_page_1 (
    .Write_Addr(multiplexer_1_out), .Write_Data(alu_1_result), .Clock(Clock), .Addr_A(register_1_q_2),
    .Addr_B(register_1_q), .Data_A(register_page_1_data_a), .Data_B(register_page_1_data_b),
    .Z(register_page_1_z), .Y(register_page_1_y), .X(register_page_1_x), .Write_Enable(Reg_WEn));
  Register #(.width(16)) register_1 (
    .D(rom_1_data), .en(IR_En), .Q({register_1_q_3, register_1_q_2, register_1_q}), .clk(Clock));  // open: clr
  ALU alu_1 (
    .Data_A(register_page_1_data_a), .Data_B(register_page_1_data_b), .Result(alu_1_result),
    .Output_enable(ALU_En), .Carry_Out(alu_1_carry_out), .Zero_Out(alu_1_zero_out),
    .Negative_Out(alu_1_negative_out), ._2s_Overflow_Out(alu_1__2s_overflow_out), .Carry_In(C),
    .Opcode(register_1_q_3));
  Multiplexer #(.select(3), .width(16), .enable("false")) multiplexer_2 (
    .in0(register_page_1_x), .in1(register_page_1_y), .in2(register_page_1_z),
    .in3({register_1_q_3, register_1_q_2, register_1_q}), .in4(undriven), .in7(counter_1_q),
    .out(multiplexer_2_out), .sel(Addr_Sel));  // open: in5, in6
  D_Flip_Flop Carry (.clk(Clock), .D(alu_1__2s_overflow_out), .Q(C), .en(Cen));  // open: Qn, preset, reset
  not not_1 (not_1_out, Clock);
  D_Flip_Flop Negative (.clk(Clock), .D(alu_1_zero_out), .Q(N), .en(Nen));  // open: Qn, preset, reset
  Control control_1 (
    .Opcode(register_1_q_3), .ALU_En(ALU_En), .Ram_Load(Ram_Load), .Ram_Store(Ram_Store),
    .Reg_In_Sel(Reg_In_Sel), .Addr_Sel(Addr_Sel), .Cen(Cen), .Nen(Nen), .Zen(Zen), .Ven(Ven),
    .PC_Load(PC_Load), .PC_En(PC_En), .Reg_WEn(Reg_WEn), .Clock(not_1_out), .IR_En(IR_En));
  D_Flip_Flop Zero (.clk(Clock), .D(alu_1_negative_out), .Q(Z), .en(Zen));  // open: Qn, preset, reset
  D_Flip_Flop _2s_Overflow (.clk(Clock), .D(alu_1_carry_out), .Q(V), .en(Ven));  // open: Qn, preset, reset
  RAM #(.addrWidth(16), .bus("separate")) ram_1 (
    .addr(multiplexer_2_out), .din(alu_1_result), .data(alu_1_result), .str(Ram_Store), .clk(Clock),
    .ld(Ram_Load));  // open: sel, clr

  // Notes on the sheet:
  //   contents of rom_1 (hex, n*v repeats v):
  //   c001 400 0 4 5 6 7 8 9 a b c d e f 10
endmodule

module Register_Page (
  input  Write_Enable,
  input  [4:0] Write_Addr,
  input  [7:0] Write_Data,
  input  Clock,
  input  [4:0] Addr_A,
  input  [4:0] Addr_B,
  output [15:0] Z,
  output [15:0] Y,
  output [15:0] X,
  output [7:0] Data_A,
  output [7:0] Data_B
);

  wire demultiplexer_1_out0, demultiplexer_1_out1, demultiplexer_1_out2, demultiplexer_1_out3,
       demultiplexer_2_out0, demultiplexer_2_out1, demultiplexer_2_out2, demultiplexer_2_out3,
       demultiplexer_2_out4, demultiplexer_2_out5, demultiplexer_2_out6, demultiplexer_2_out7,
       demultiplexer_3_out0, demultiplexer_3_out1, demultiplexer_3_out2, demultiplexer_3_out3,
       demultiplexer_3_out4, demultiplexer_3_out5, demultiplexer_3_out6, demultiplexer_3_out7,
       demultiplexer_4_out0, demultiplexer_4_out1, demultiplexer_4_out2, demultiplexer_4_out3,
       demultiplexer_4_out4, demultiplexer_4_out5, demultiplexer_4_out6, demultiplexer_4_out7,
       demultiplexer_5_out0, demultiplexer_5_out1, demultiplexer_5_out2, demultiplexer_5_out3,
       demultiplexer_5_out4, demultiplexer_5_out5, demultiplexer_5_out6, demultiplexer_5_out7;
  wire [7:0] multiplexer_3_out, multiplexer_4_out, multiplexer_5_out, multiplexer_6_out, multiplexer_7_out,
       multiplexer_8_out, multiplexer_9_out, multiplexer_10_out, register_1_q, register_2_q, register_3_q,
       register_4_q, register_5_q, register_6_q, register_7_q, register_8_q, register_9_q, register_10_q,
       register_11_q, register_12_q, register_13_q, register_14_q, register_15_q, register_16_q,
       register_17_q, register_18_q, register_19_q, register_20_q, register_21_q, register_22_q,
       register_23_q, register_24_q, register_31_q, register_32_q;

  Demultiplexer #(.select(2), .enable("false")) demultiplexer_1 (
    .out0(demultiplexer_1_out0), .out1(demultiplexer_1_out1), .out2(demultiplexer_1_out2),
    .out3(demultiplexer_1_out3), .in(Write_Enable), .sel(Write_Addr[4:3]));
  Demultiplexer #(.select(3), .enable("false")) demultiplexer_2 (
    .out0(demultiplexer_2_out0), .out1(demultiplexer_2_out1), .out2(demultiplexer_2_out2),
    .out3(demultiplexer_2_out3), .out4(demultiplexer_2_out4), .out5(demultiplexer_2_out5),
    .out6(demultiplexer_2_out6), .out7(demultiplexer_2_out7), .in(demultiplexer_1_out0), .sel(Write_Addr[2:0]));
  Multiplexer #(.select(2), .width(8), .enable("false")) multiplexer_1 (
    .in0(multiplexer_3_out), .in1(multiplexer_5_out), .in2(multiplexer_7_out), .in3(multiplexer_9_out),
    .out(Data_A), .sel(Addr_A[4:3]));
  Multiplexer #(.select(2), .width(8), .enable("false")) multiplexer_2 (
    .in0(multiplexer_4_out), .in1(multiplexer_6_out), .in2(multiplexer_8_out), .in3(multiplexer_10_out),
    .out(Data_B), .sel(Addr_B[4:3]));
  Register register_1 (.D(Write_Data), .en(demultiplexer_2_out7), .Q(register_1_q), .clk(Clock));  // open: clr
  Register register_2 (.D(Write_Data), .en(demultiplexer_2_out6), .Q(register_2_q), .clk(Clock));  // open: clr
  Register register_3 (.D(Write_Data), .en(demultiplexer_2_out5), .Q(register_3_q), .clk(Clock));  // open: clr
  Register register_4 (.D(Write_Data), .en(demultiplexer_2_out4), .Q(register_4_q), .clk(Clock));  // open: clr
  Register register_5 (.D(Write_Data), .en(demultiplexer_2_out3), .Q(register_5_q), .clk(Clock));  // open: clr
  Register register_6 (.D(Write_Data), .en(demultiplexer_2_out2), .Q(register_6_q), .clk(Clock));  // open: clr
  Register register_7 (.D(Write_Data), .en(demultiplexer_2_out1), .Q(register_7_q), .clk(Clock));  // open: clr
  Register register_8 (.D(Write_Data), .en(demultiplexer_2_out0), .Q(register_8_q), .clk(Clock));  // open: clr
  Multiplexer #(.select(3), .width(8), .enable("false")) multiplexer_3 (
    .in0(register_8_q), .in1(register_7_q), .in2(register_6_q), .in3(register_5_q), .in4(register_4_q),
    .in5(register_3_q), .in6(register_2_q), .in7(register_1_q), .out(multiplexer_3_out), .sel(Addr_A[2:0]));
  Multiplexer #(.select(3), .width(8), .enable("false")) multiplexer_4 (
    .in0(register_8_q), .in1(register_7_q), .in2(register_6_q), .in3(register_5_q), .in4(register_4_q),
    .in5(register_3_q), .in6(register_2_q), .in7(register_1_q), .out(multiplexer_4_out), .sel(Addr_B[2:0]));
  Demultiplexer #(.select(3), .enable("false")) demultiplexer_3 (
    .out0(demultiplexer_3_out0), .out1(demultiplexer_3_out1), .out2(demultiplexer_3_out2),
    .out3(demultiplexer_3_out3), .out4(demultiplexer_3_out4), .out5(demultiplexer_3_out5),
    .out6(demultiplexer_3_out6), .out7(demultiplexer_3_out7), .in(demultiplexer_1_out1), .sel(Write_Addr[2:0]));
  Register register_9 (.D(Write_Data), .en(demultiplexer_3_out7), .Q(register_9_q), .clk(Clock));  // open: clr
  Register register_10 (.D(Write_Data), .en(demultiplexer_3_out6), .Q(register_10_q), .clk(Clock));  // open: clr
  Register register_11 (.D(Write_Data), .en(demultiplexer_3_out5), .Q(register_11_q), .clk(Clock));  // open: clr
  Register register_12 (.D(Write_Data), .en(demultiplexer_3_out4), .Q(register_12_q), .clk(Clock));  // open: clr
  Register register_13 (.D(Write_Data), .en(demultiplexer_3_out3), .Q(register_13_q), .clk(Clock));  // open: clr
  Register register_14 (.D(Write_Data), .en(demultiplexer_3_out2), .Q(register_14_q), .clk(Clock));  // open: clr
  Register register_15 (.D(Write_Data), .en(demultiplexer_3_out1), .Q(register_15_q), .clk(Clock));  // open: clr
  Register register_16 (.D(Write_Data), .en(demultiplexer_3_out0), .Q(register_16_q), .clk(Clock));  // open: clr
  Multiplexer #(.select(3), .width(8), .enable("false")) multiplexer_5 (
    .in0(register_16_q), .in1(register_15_q), .in2(register_14_q), .in3(register_13_q), .in4(register_12_q),
    .in5(register_11_q), .in6(register_10_q), .in7(register_9_q), .out(multiplexer_5_out), .sel(Addr_A[2:0]));
  Multiplexer #(.select(3), .width(8), .enable("false")) multiplexer_6 (
    .in0(register_16_q), .in1(register_15_q), .in2(register_14_q), .in3(register_13_q), .in4(register_12_q),
    .in5(register_11_q), .in6(register_10_q), .in7(register_9_q), .out(multiplexer_6_out), .sel(Addr_B[2:0]));
  Demultiplexer #(.select(3), .enable("false")) demultiplexer_4 (
    .out0(demultiplexer_4_out0), .out1(demultiplexer_4_out1), .out2(demultiplexer_4_out2),
    .out3(demultiplexer_4_out3), .out4(demultiplexer_4_out4), .out5(demultiplexer_4_out5),
    .out6(demultiplexer_4_out6), .out7(demultiplexer_4_out7), .in(demultiplexer_1_out2), .sel(Write_Addr[2:0]));
  Register register_17 (.D(Write_Data), .en(demultiplexer_4_out7), .Q(register_17_q), .clk(Clock));  // open: clr
  Register register_18 (.D(Write_Data), .en(demultiplexer_4_out6), .Q(register_18_q), .clk(Clock));  // open: clr
  Register register_19 (.D(Write_Data), .en(demultiplexer_4_out5), .Q(register_19_q), .clk(Clock));  // open: clr
  Register register_20 (.D(Write_Data), .en(demultiplexer_4_out4), .Q(register_20_q), .clk(Clock));  // open: clr
  Register register_21 (.D(Write_Data), .en(demultiplexer_4_out3), .Q(register_21_q), .clk(Clock));  // open: clr
  Register register_22 (.D(Write_Data), .en(demultiplexer_4_out2), .Q(register_22_q), .clk(Clock));  // open: clr
  Register register_23 (.D(Write_Data), .en(demultiplexer_4_out1), .Q(register_23_q), .clk(Clock));  // open: clr
  Register register_24 (.D(Write_Data), .en(demultiplexer_4_out0), .Q(register_24_q), .clk(Clock));  // open: clr
  Multiplexer #(.select(3), .width(8), .enable("false")) multiplexer_7 (
    .in0(register_24_q), .in1(register_23_q), .in2(register_22_q), .in3(register_21_q), .in4(register_20_q),
    .in5(register_19_q), .in6(register_18_q), .in7(register_17_q), .out(multiplexer_7_out), .sel(Addr_A[2:0]));
  Multiplexer #(.select(3), .width(8), .enable("false")) multiplexer_8 (
    .in0(register_24_q), .in1(register_23_q), .in2(register_22_q), .in3(register_21_q), .in4(register_20_q),
    .in5(register_19_q), .in6(register_18_q), .in7(register_17_q), .out(multiplexer_8_out), .sel(Addr_B[2:0]));
  Demultiplexer #(.select(3), .enable("false")) demultiplexer_5 (
    .out0(demultiplexer_5_out0), .out1(demultiplexer_5_out1), .out2(demultiplexer_5_out2),
    .out3(demultiplexer_5_out3), .out4(demultiplexer_5_out4), .out5(demultiplexer_5_out5),
    .out6(demultiplexer_5_out6), .out7(demultiplexer_5_out7), .in(demultiplexer_1_out3), .sel(Write_Addr[2:0]));
  Register register_25 (.D(Write_Data), .en(demultiplexer_5_out7), .Q(Z[7:0]), .clk(Clock));  // open: clr
  Register register_26 (.D(Write_Data), .en(demultiplexer_5_out6), .Q(Z[15:8]), .clk(Clock));  // open: clr
  Register register_27 (.D(Write_Data), .en(demultiplexer_5_out5), .Q(Y[7:0]), .clk(Clock));  // open: clr
  Register register_28 (.D(Write_Data), .en(demultiplexer_5_out4), .Q(Y[15:8]), .clk(Clock));  // open: clr
  Register register_29 (.D(Write_Data), .en(demultiplexer_5_out3), .Q(X[7:0]), .clk(Clock));  // open: clr
  Register register_30 (.D(Write_Data), .en(demultiplexer_5_out2), .Q(X[15:8]), .clk(Clock));  // open: clr
  Register register_31 (.D(Write_Data), .en(demultiplexer_5_out1), .Q(register_31_q), .clk(Clock));  // open: clr
  Register register_32 (.D(Write_Data), .en(demultiplexer_5_out0), .Q(register_32_q), .clk(Clock));  // open: clr
  Multiplexer #(.select(3), .width(8), .enable("false")) multiplexer_9 (
    .in0(register_32_q), .in1(register_31_q), .in2(X[15:8]), .in3(X[7:0]), .in4(Y[15:8]), .in5(Y[7:0]),
    .in6(Z[15:8]), .in7(Z[7:0]), .out(multiplexer_9_out), .sel(Addr_A[2:0]));
  Multiplexer #(.select(3), .width(8), .enable("false")) multiplexer_10 (
    .in0(register_32_q), .in1(register_31_q), .in2(X[15:8]), .in3(X[7:0]), .in4(Y[15:8]), .in5(Y[7:0]),
    .in6(Z[15:8]), .in7(Z[7:0]), .out(multiplexer_10_out), .sel(Addr_B[2:0]));
endmodule

module ALU (
  input  Output_enable,
  input  [5:0] Opcode,
  input  Carry_In,
  input  [7:0] Data_A,
  input  [7:0] Data_B,
  output [7:0] Result,
  output _2s_Overflow_Out,
  output Carry_Out,
  output Negative_Out,
  output Zero_Out
);

  wire [6:0] Result_t;

  assign Result = Output_enable ? {Negative_Out, Result_t} : 8'bz;  // Controlled_Buffer controlled_buffer_1
  Adder adder_1 (.a(Data_A), .b(Data_B), .out({Negative_Out, Result_t}), .cin(Carry_In), .cout(Carry_Out));
  Comparator comparator_1 (.a({Negative_Out, Result_t}), .b({8{1'b0}}), .eq(Zero_Out));  // open: gt, lt

  assign _2s_Overflow_Out = 1'b0;

  // Other names for the same wires on the sheet: Result_t[7] = Negative_Out
endmodule

module Control (
  input  [5:0] Opcode,
  input  Clock,
  output ALU_En,
  output Ram_Load,
  output Ram_Store,
  output Reg_In_Sel,
  output [2:0] Addr_Sel,
  output Cen,
  output Nen,
  output Zen,
  output Ven,
  output PC_Load,
  output PC_En,
  output Reg_WEn,
  output IR_En
);

  wire [3:0] Main_NS, multiplexer_1_out, multiplexer_2_out, multiplexer_4_out, State, undriven, undriven_2,
       undriven_3, undriven_4;
  wire [15:0] Decode_state, Fetch_state, JMP_Fetch, JMP_Load, undriven_5, undriven_6, undriven_7, undriven_8,
       undriven_9, undriven_10, undriven_11, undriven_12, undriven_13, undriven_14, undriven_15;
  wire [15:1] ALU_State;
  wire [15:15] pull_resistor_1_node;

  Multiplexer #(.select(5), .width(4), .enable("false")) multiplexer_1 (
    .in0(4'b1000), .in1(4'b0110), .out(multiplexer_1_out), .sel(Opcode[4:0]));  // open: in2, in3, in4, in5, in6, in7, in8, in9, in10, in11, in12, in13, in14, in15, in16, in17, in18, in19, in20, in21, in22, in23, in24, in25, in26, in27, in28, in29, in30, in31
  Multiplexer #(.select(5), .width(4), .enable("false")) multiplexer_2 (
    .in16(4'b1001), .out(multiplexer_2_out), .sel(Opcode[4:0]));  // open: in0, in1, in2, in3, in4, in5, in6, in7, in8, in9, in10, in11, in12, in13, in14, in15, in17, in18, in19, in20, in21, in22, in23, in24, in25, in26, in27, in28, in29, in30, in31
  Multiplexer #(.width(4), .enable("false")) multiplexer_3 (
    .in0(multiplexer_1_out), .in1(multiplexer_2_out), .out(Main_NS), .sel(Opcode[5]));
  Multiplexer #(.select(4), .width(4), .enable("false")) multiplexer_4 (
    .in0(4'b0111), .in1(undriven), .in2(undriven_2), .in3(undriven_3), .in4(undriven_4), .in5(4'b0111),
    .in6(4'b0101), .in7(4'b1000), .in8(Main_NS), .in9(4'b0111), .out(multiplexer_4_out), .sel(State));  // open: in10, in11, in12, in13, in14, in15
  Register #(.width(4)) register_1 (.D(multiplexer_4_out), .Q(State), .clk(Clock));  // open: en, clr
  Pull_Resistor pull_resistor_1 (.node({pull_resistor_1_node[15], IR_En, Reg_WEn, PC_En, PC_Load, Ven, Zen, Nen, Cen, Addr_Sel, Reg_In_Sel, Ram_Store, Ram_Load, ALU_En}));
  Multiplexer #(.select(4), .width(16), .enable("false")) multiplexer_5 (
    .in0(undriven_5), .in1(undriven_6), .in2(undriven_7), .in3(undriven_8), .in4(undriven_9),
    .in5({JMP_Load[15:12], 1'b1, JMP_Load[10:7], 3'b011, JMP_Load[3:0]}),
    .in6({JMP_Fetch[15], 1'b1, JMP_Fetch[13:0]}), .in7({Fetch_state[15], 1'b1, Fetch_state[13:0]}),
    .in8({Decode_state[15:13], 1'b1, Decode_state[11:0]}),
    .in9({ALU_State[15:14], 1'b1, ALU_State[12:1], 1'b1}), .in10(undriven_10), .in11(undriven_11),
    .in12(undriven_12), .in13(undriven_13), .in14(undriven_14), .in15(undriven_15),
    .out({pull_resistor_1_node[15], IR_En, Reg_WEn, PC_En, PC_Load, Ven, Zen, Nen, Cen, Addr_Sel, Reg_In_Sel, Ram_Store, Ram_Load, ALU_En}),
    .sel(State));
endmodule

module Call_stack (
  input  Pop,
  input  Push,
  input  Clock,
  input  [15:0] Address
);

  wire or_1_out;
  wire [7:0] counter_1_q;
  wire [15:0] ram_1_data;

  or or_1 (or_1_out, Pop, Push);
  Counter #(.trigger("falling")) counter_1 (
    .load(Pop), .count(or_1_out), .Q(counter_1_q), .clk(Clock));  // open: D, carry, clr
  Register #(.width(16)) register_1 (.D(ram_1_data), .en(Pop), .clk(Clock));  // open: Q, clr
  RAM #(.dataWidth(16), .bus("separate")) ram_1 (
    .addr(counter_1_q), .din(Address), .data(ram_1_data), .str(Push), .clk(Clock));  // open: sel, ld, clr
endmodule
