// Logisim project WolfCPU3.circ as structural Verilog: 3 circuits, main circuit main
module main (
  input  in_1,
  input  in_2
);

  wire clock_1_out, Clock_A, Clock_B, decoder_1_out0, decoder_1_out1, decoder_1_out2, decoder_1_out3,
       decoder_1_out4, decoder_2_out0, decoder_2_out3, decoder_4_out0, decoder_4_out2, decoder_4_out4,
       decoder_4_out6, decoder_4_out7, Next_Instruction, not_1_out, not_2_out, not_4_out, not_5_out,
       or_1_out, Write_enable;
  wire [2:0] counter_2_q;
  wire [3:0] counter_1_q;
  wire [4:0] RA, RB;
  wire [5:0] OPCODE;
  wire [15:0] A, B, BVal, \byte , controlled_buffer_1_out, controlled_buffer_7_out, IMM, PC_q, Ram_Out,
       Ramaddr, Result, SEbyte, Value;

  Clock clock_1 (.out(clock_1_out));
  Counter #(.width(16), .max('hffff)) PC (.count(or_1_out), .Q(PC_q), .clk(Clock_A));  // open: load, D, carry, clr
  not not_1 (not_1_out, decoder_1_out4);
  Counter #(.width(4), .max('hf)) counter_1 (
    .Q(counter_1_q), .clk(Clock_B), .clr(Next_Instruction));  // open: load, D, count, carry
  and and_1 (Clock_A, clock_1_out, ~in_1);  // AND_Gate
  assign controlled_buffer_1_out = not_2_out ? Ramaddr : 16'bz;  // Controlled_Buffer controlled_buffer_1
  assign controlled_buffer_1_out = not_1_out ? PC_q : 16'bz;  // Controlled_Buffer controlled_buffer_2
  not not_2 (not_2_out, not_1_out);
  or or_1 (or_1_out, decoder_1_out1, decoder_1_out3);
  Counter #(.width(3), .max('h7)) counter_2 (
    .count(not_1_out), .Q(counter_2_q), .clk(Clock_B), .clr(Next_Instruction));  // open: load, D, carry
  Decoder #(.select(3)) decoder_1 (
    .out0(decoder_1_out0), .out1(decoder_1_out1), .out2(decoder_1_out2), .out3(decoder_1_out3),
    .out4(decoder_1_out4), .sel(counter_2_q));  // open: out5, out6, out7, en
  Decoder #(.select(2)) decoder_2 (
    .out0(decoder_2_out0), .out3(decoder_2_out3), .sel(OPCODE[5:4]));  // open: out1, out2, en
  Decoder #(.select(4)) decoder_3 (
    .out4(Write_enable), .out5(Next_Instruction), .sel(counter_1_q));  // open: out0, out1, out2, out3, out6, out7, out8, out9, out10, out11, out12, out13, out14, out15, en
  not not_3 (Clock_B, Clock_A);
  RAM #(.addrWidth(16), .dataWidth(16), .bus("separate")) ram_1 (
    .addr(controlled_buffer_1_out), .data(Ram_Out), .str(in_2), .clk(Clock_A), .ld(1'b1));  // open: din, sel, clr
  assign BVal = decoder_2_out0 ? B : 16'bz;  // Controlled_Buffer controlled_buffer_3
  not not_4 (not_4_out, decoder_2_out0);
  assign BVal = not_4_out ? IMM : 16'bz;  // Controlled_Buffer controlled_buffer_4
  Decoder #(.select(3), .tristate("true")) decoder_4 (
    .out0(decoder_4_out0), .out1(decoder_4_out0), .out2(decoder_4_out2), .out3(decoder_4_out2),
    .out4(decoder_4_out4), .out5(decoder_4_out4), .out6(decoder_4_out6), .out7(decoder_4_out7),
    .sel(OPCODE[2:0]));  // open: en
  Register #(.width(16)) register_1 (.D(Ram_Out), .en(decoder_1_out2), .Q(IMM), .clk(Clock_A));  // open: clr
  Register #(.width(16)) register_2 (
    .D(Ram_Out), .en(decoder_1_out0), .Q({OPCODE, RA, RB}), .clk(Clock_A));  // open: clr
  Pull_Resistor pull_resistor_1 (.node(decoder_4_out0));
  Pull_Resistor pull_resistor_2 (.node(decoder_4_out2));
  Pull_Resistor pull_resistor_3 (.node(decoder_4_out6));
  Pull_Resistor pull_resistor_4 (.node(decoder_4_out7));
  Pull_Resistor pull_resistor_5 (.node(decoder_4_out4));
  assign \byte  = {{8{1'b0}}, Ram_Out[7:0]};  // Bit_Extender bit_extender_1
  assign SEbyte = {{8{Ram_Out[7]}}, Ram_Out[7:0]};  // Bit_Extender bit_extender_2
  Register_Unit register_unit_1 (
    .Addr_A(RB), .Addr_B(IMM[15:11]), .Write_Enable(Write_enable), .Addr_W(RA), .in_5(Value), .in_6(Clock_A),
    .out_7(A), .out_8(B));
  assign Value = not_5_out ? Result : 16'bz;  // Controlled_Buffer controlled_buffer_5
  not not_5 (not_5_out, decoder_2_out3);
  assign Value = decoder_2_out3 ? controlled_buffer_7_out : 16'bz;  // Controlled_Buffer controlled_buffer_6
  assign controlled_buffer_7_out = decoder_4_out0 ? SEbyte : 16'bz;  // Controlled_Buffer controlled_buffer_7
  assign controlled_buffer_7_out = decoder_4_out2 ? \byte  : 16'bz;  // Controlled_Buffer controlled_buffer_8
  assign controlled_buffer_7_out = decoder_4_out6 ? B : 16'bz;  // Controlled_Buffer controlled_buffer_9
  assign controlled_buffer_7_out = decoder_4_out7 ? IMM : 16'bz;  // Controlled_Buffer controlled_buffer_10
  assign controlled_buffer_7_out = decoder_4_out4 ? Ram_Out : 16'bz;  // Controlled_Buffer controlled_buffer_11
  ALU alu_1 (.in_1(OPCODE), .in_2(A), .in_3(BVal), .out_4(Result));

  // Other names for the same wires on the sheet: RC[4:0] = IMM[15:11]
endmodule

module ALU (
  input  [5:0] in_1,
  input  [15:0] in_2,
  input  [15:0] in_3,
  output [15:0] out_4
);

  wire comparator_1_eq, comparator_1_gt, comparator_1_lt, comparator_2_gt, comparator_2_lt, not_2_out,
       not_3_out, not_4_out, not_5_out;
  wire [15:0] Add, And, controlled_buffer_1_out, controlled_buffer_2_out, controlled_buffer_5_out,
       controlled_buffer_7_out, controlled_buffer_8_out, controlled_buffer_10_out, controlled_buffer_13_out,
       controlled_buffer_14_out, controlled_buffer_17_out, controlled_buffer_19_out,
       controlled_buffer_20_out, controlled_buffer_22_out, controlled_buffer_25_out,
       controlled_buffer_27_out, Div, EQ, GTS, GTU, Left, LTS, LTU, Mult, Not, Or, RightA, RightL, Sub, Xor;

  Adder #(.width(16)) adder_1 (.a(in_2), .b(in_3), .out(Add));  // open: cin, cout
  Subtractor #(.width(16)) subtractor_1 (.a(in_2), .b(in_3), .out(Sub));  // open: bin, bout
  Multiplier #(.width(16)) multiplier_1 (.a(in_2), .b(in_3), .out(Mult));  // open: cin, cout
  Divider #(.width(16)) divider_1 (.a(in_2), .b(in_3), .out(Div));  // open: upper, rem
  Shifter #(.width(16)) shifter_1 (.in(in_2), .\dist (in_3[3:0]), .out(Left));
  Shifter #(.width(16), .shift("lr")) shifter_2 (.in(in_2), .\dist (in_3[3:0]), .out(RightL));
  Shifter #(.width(16), .shift("ar")) shifter_3 (.in(in_2), .\dist (in_3[3:0]), .out(RightA));
  assign And = in_2 & in_3;  // AND_Gate and_1, 16 bits wide
  assign Or = in_2 | in_3;  // OR_Gate or_1, 16 bits wide
  assign Xor = in_2 ^ in_3;  // XOR_Gate xor_1, 16 bits wide
  assign Not = ~in_2;  // NOT_Gate not_1, 16 bits wide
  Comparator #(.width(16), .mode("unsigned")) comparator_1 (
    .a(in_2), .b(in_3), .gt(comparator_1_gt), .eq(comparator_1_eq), .lt(comparator_1_lt));
  Comparator #(.width(16)) comparator_2 (.a(in_2), .b(in_3), .gt(comparator_2_gt), .lt(comparator_2_lt));  // open: eq
  not not_2 (not_2_out, in_1[0]);
  assign GTU = {{15{1'b0}}, comparator_1_gt};  // Bit_Extender bit_extender_1
  assign EQ = {{15{1'b0}}, comparator_1_eq};  // Bit_Extender bit_extender_2
  assign LTU = {{15{1'b0}}, comparator_1_lt};  // Bit_Extender bit_extender_3
  assign GTS = {{15{1'b0}}, comparator_2_gt};  // Bit_Extender bit_extender_4
  assign LTS = {{15{1'b0}}, comparator_2_lt};  // Bit_Extender bit_extender_5
  not not_3 (not_3_out, in_1[1]);
  assign controlled_buffer_1_out = not_2_out ? Add : 16'bz;  // Controlled_Buffer controlled_buffer_1
  assign controlled_buffer_2_out = not_3_out ? controlled_buffer_1_out : 16'bz;  // Controlled_Buffer controlled_buffer_2
  assign controlled_buffer_1_out = in_1[0] ? Sub : 16'bz;  // Controlled_Buffer controlled_buffer_3
  assign controlled_buffer_2_out = in_1[1] ? controlled_buffer_5_out : 16'bz;  // Controlled_Buffer controlled_buffer_4
  assign controlled_buffer_5_out = not_2_out ? Not : 16'bz;  // Controlled_Buffer controlled_buffer_5
  assign controlled_buffer_5_out = in_1[0] ? GTS : 16'bz;  // Controlled_Buffer controlled_buffer_6
  assign controlled_buffer_7_out = not_2_out ? And : 16'bz;  // Controlled_Buffer controlled_buffer_7
  assign controlled_buffer_8_out = not_3_out ? controlled_buffer_7_out : 16'bz;  // Controlled_Buffer controlled_buffer_8
  assign controlled_buffer_7_out = in_1[0] ? Or : 16'bz;  // Controlled_Buffer controlled_buffer_9
  assign controlled_buffer_10_out = not_2_out ? Xor : 16'bz;  // Controlled_Buffer controlled_buffer_10
  assign controlled_buffer_8_out = in_1[1] ? controlled_buffer_10_out : 16'bz;  // Controlled_Buffer controlled_buffer_11
  assign controlled_buffer_10_out = in_1[0] ? GTU : 16'bz;  // Controlled_Buffer controlled_buffer_12
  assign controlled_buffer_13_out = not_3_out ? controlled_buffer_14_out : 16'bz;  // Controlled_Buffer controlled_buffer_13
  assign controlled_buffer_14_out = not_2_out ? Mult : 16'bz;  // Controlled_Buffer controlled_buffer_14
  assign controlled_buffer_14_out = in_1[0] ? Div : 16'bz;  // Controlled_Buffer controlled_buffer_15
  assign controlled_buffer_13_out = in_1[1] ? controlled_buffer_17_out : 16'bz;  // Controlled_Buffer controlled_buffer_16
  assign controlled_buffer_17_out = not_2_out ? LTS : 16'bz;  // Controlled_Buffer controlled_buffer_17
  assign controlled_buffer_17_out = in_1[0] ? LTU : 16'bz;  // Controlled_Buffer controlled_buffer_18
  assign controlled_buffer_19_out = not_2_out ? Left : 16'bz;  // Controlled_Buffer controlled_buffer_19
  assign controlled_buffer_20_out = not_3_out ? controlled_buffer_19_out : 16'bz;  // Controlled_Buffer controlled_buffer_20
  assign controlled_buffer_19_out = in_1[0] ? RightL : 16'bz;  // Controlled_Buffer controlled_buffer_21
  assign controlled_buffer_22_out = not_2_out ? RightA : 16'bz;  // Controlled_Buffer controlled_buffer_22
  assign controlled_buffer_20_out = in_1[1] ? controlled_buffer_22_out : 16'bz;  // Controlled_Buffer controlled_buffer_23
  assign controlled_buffer_22_out = in_1[0] ? EQ : 16'bz;  // Controlled_Buffer controlled_buffer_24
  not not_4 (not_4_out, in_1[3]);
  not not_5 (not_5_out, in_1[2]);
  assign controlled_buffer_25_out = not_5_out ? controlled_buffer_2_out : 16'bz;  // Controlled_Buffer controlled_buffer_25
  assign controlled_buffer_25_out = in_1[2] ? controlled_buffer_8_out : 16'bz;  // Controlled_Buffer controlled_buffer_26
  assign controlled_buffer_27_out = not_5_out ? controlled_buffer_13_out : 16'bz;  // Controlled_Buffer controlled_buffer_27
  assign controlled_buffer_27_out = in_1[2] ? controlled_buffer_20_out : 16'bz;  // Controlled_Buffer controlled_buffer_28
  assign out_4 = not_4_out ? controlled_buffer_25_out : 16'bz;  // Controlled_Buffer controlled_buffer_29
  assign out_4 = in_1[3] ? controlled_buffer_27_out : 16'bz;  // Controlled_Buffer controlled_buffer_30

  // Other names for the same wires on the sheet: Op_A[15:0] = in_2; Op_B[15:0] = in_3
endmodule

module Register_Unit (
  input  [4:0] Addr_A,
  input  [4:0] Addr_B,
  input  Write_Enable,
  input  [4:0] Addr_W,
  input  [15:0] in_5,
  input  in_6,
  output [15:0] out_7,
  output [15:0] out_8
);

  wire [7:0] Bank_1A, Bank_1B, Bank_2A, Bank_2B, Bank_3A, Bank_3B, Bank_4A, Bank_4B, Store_1, Store_2,
       Store_3, Store_4;
  wire [15:0] register_1_q, register_2_q, register_3_q, register_4_q, register_5_q, register_6_q,
       register_7_q, register_8_q, register_9_q, register_10_q, register_11_q, register_12_q, register_13_q,
       register_14_q, register_15_q, register_16_q, register_17_q, register_18_q, register_19_q,
       register_20_q, register_21_q, register_22_q, register_23_q, register_24_q, register_25_q,
       register_26_q, register_27_q, register_28_q, register_29_q, register_30_q, register_31_q,
       register_32_q;

  Decoder #(.select(5)) decoder_1 (
    .out0(Bank_1A[7]), .out1(Bank_1A[6]), .out2(Bank_1A[5]), .out3(Bank_1A[4]), .out4(Bank_1A[3]),
    .out5(Bank_1A[2]), .out6(Bank_1A[1]), .out7(Bank_1A[0]), .out8(Bank_2A[7]), .out9(Bank_2A[6]),
    .out10(Bank_2A[5]), .out11(Bank_2A[4]), .out12(Bank_2A[3]), .out13(Bank_2A[2]), .out14(Bank_2A[1]),
    .out15(Bank_2A[0]), .out16(Bank_3A[7]), .out17(Bank_3A[6]), .out18(Bank_3A[5]), .out19(Bank_3A[4]),
    .out20(Bank_3A[3]), .out21(Bank_3A[2]), .out22(Bank_3A[1]), .out23(Bank_3A[0]), .out24(Bank_4A[7]),
    .out25(Bank_4A[6]), .out26(Bank_4A[5]), .out27(Bank_4A[4]), .out28(Bank_4A[3]), .out29(Bank_4A[2]),
    .out30(Bank_4A[1]), .out31(Bank_4A[0]), .sel(Addr_A));  // open: en
  Decoder #(.select(5)) decoder_2 (
    .out0(Bank_1B[7]), .out1(Bank_1B[6]), .out2(Bank_1B[5]), .out3(Bank_1B[4]), .out4(Bank_1B[3]),
    .out5(Bank_1B[2]), .out6(Bank_1B[1]), .out7(Bank_1B[0]), .out8(Bank_2B[7]), .out9(Bank_2B[6]),
    .out10(Bank_2B[5]), .out11(Bank_2B[4]), .out12(Bank_2B[3]), .out13(Bank_2B[2]), .out14(Bank_2B[1]),
    .out15(Bank_2B[0]), .out16(Bank_3B[7]), .out17(Bank_3B[6]), .out18(Bank_3B[5]), .out19(Bank_3B[4]),
    .out20(Bank_3B[3]), .out21(Bank_3B[2]), .out22(Bank_3B[1]), .out23(Bank_3B[0]), .out24(Bank_4B[7]),
    .out25(Bank_4B[6]), .out26(Bank_4B[5]), .out27(Bank_4B[4]), .out28(Bank_4B[3]), .out29(Bank_4B[2]),
    .out30(Bank_4B[1]), .out31(Bank_4B[0]), .sel(Addr_B));  // open: en
  Decoder #(.select(5), .disabled(0)) decoder_3 (
    .out0(Store_1[7]), .out1(Store_1[6]), .out2(Store_1[5]), .out3(Store_1[4]), .out4(Store_1[3]),
    .out5(Store_1[2]), .out6(Store_1[1]), .out7(Store_1[0]), .out8(Store_2[7]), .out9(Store_2[6]),
    .out10(Store_2[5]), .out11(Store_2[4]), .out12(Store_2[3]), .out13(Store_2[2]), .out14(Store_2[1]),
    .out15(Store_2[0]), .out16(Store_3[7]), .out17(Store_3[6]), .out18(Store_3[5]), .out19(Store_3[4]),
    .out20(Store_3[3]), .out21(Store_3[2]), .out22(Store_3[1]), .out23(Store_3[0]), .out24(Store_4[7]),
    .out25(Store_4[6]), .out26(Store_4[5]), .out27(Store_4[4]), .out28(Store_4[3]), .out29(Store_4[2]),
    .out30(Store_4[1]), .out31(Store_4[0]), .sel(Addr_W), .en(Write_Enable));
  Register #(.width(16)) register_1 (.D(in_5), .en(Store_1[7]), .Q(register_1_q), .clk(in_6));  // open: clr
  Register #(.width(16)) register_2 (.D(in_5), .en(Store_1[6]), .Q(register_2_q), .clk(in_6));  // open: clr
  Register #(.width(16)) register_3 (.D(in_5), .en(Store_1[5]), .Q(register_3_q), .clk(in_6));  // open: clr
  Register #(.width(16)) register_4 (.D(in_5), .en(Store_1[4]), .Q(register_4_q), .clk(in_6));  // open: clr
  Register #(.width(16)) register_5 (.D(in_5), .en(Store_1[3]), .Q(register_5_q), .clk(in_6));  // open: clr
  Register #(.width(16)) register_6 (.D(in_5), .en(Store_1[2]), .Q(register_6_q), .clk(in_6));  // open: clr
  Register #(.width(16)) register_7 (.D(in_5), .en(Store_1[1]), .Q(register_7_q), .clk(in_6));  // open: clr
  Register #(.width(16)) register_8 (.D(in_5), .en(Store_1[0]), .Q(register_8_q), .clk(in_6));  // open: clr
  assign out_7 = Bank_1A[7] ? register_1_q : 16'bz;  // Controlled_Buffer controlled_buffer_1
  assign out_8 = Bank_1B[7] ? register_1_q : 16'bz;  // Controlled_Buffer controlled_buffer_2
  assign out_7 = Bank_1A[6] ? register_2_q : 16'bz;  // Controlled_Buffer controlled_buffer_3
  assign out_8 = Bank_1B[6] ? register_2_q : 16'bz;  // Controlled_Buffer controlled_buffer_4
  assign out_7 = Bank_1A[5] ? register_3_q : 16'bz;  // Controlled_Buffer controlled_buffer_5
  assign out_8 = Bank_1B[5] ? register_3_q : 16'bz;  // Controlled_Buffer controlled_buffer_6
  assign out_7 = Bank_1A[4] ? register_4_q : 16'bz;  // Controlled_Buffer controlled_buffer_7
  assign out_8 = Bank_1B[4] ? register_4_q : 16'bz;  // Controlled_Buffer controlled_buffer_8
  assign out_7 = Bank_1A[3] ? register_5_q : 16'bz;  // Controlled_Buffer controlled_buffer_9
  assign out_8 = Bank_1B[3] ? register_5_q : 16'bz;  // Controlled_Buffer controlled_buffer_10
  assign out_7 = Bank_1A[2] ? register_6_q : 16'bz;  // Controlled_Buffer controlled_buffer_11
  assign out_8 = Bank_1B[2] ? register_6_q : 16'bz;  // Controlled_Buffer controlled_buffer_12
  assign out_7 = Bank_1A[1] ? register_7_q : 16'bz;  // Controlled_Buffer controlled_buffer_13
  assign out_8 = Bank_1B[1] ? register_7_q : 16'bz;  // Controlled_Buffer controlled_buffer_14
  assign out_7 = Bank_1A[0] ? register_8_q : 16'bz;  // Controlled_Buffer controlled_buffer_15
  assign out_8 = Bank_1B[0] ? register_8_q : 16'bz;  // Controlled_Buffer controlled_buffer_16
  Register #(.width(16)) register_9 (.D(in_5), .en(Store_2[0]), .Q(register_9_q), .clk(in_6));  // open: clr
  Register #(.width(16)) register_10 (.D(in_5), .en(Store_2[1]), .Q(register_10_q), .clk(in_6));  // open: clr
  Register #(.width(16)) register_11 (.D(in_5), .en(Store_2[2]), .Q(register_11_q), .clk(in_6));  // open: clr
  Register #(.width(16)) register_12 (.D(in_5), .en(Store_2[3]), .Q(register_12_q), .clk(in_6));  // open: clr
  Register #(.width(16)) register_13 (.D(in_5), .en(Store_2[4]), .Q(register_13_q), .clk(in_6));  // open: clr
  Register #(.width(16)) register_14 (.D(in_5), .en(Store_2[5]), .Q(register_14_q), .clk(in_6));  // open: clr
  Register #(.width(16)) register_15 (.D(in_5), .en(Store_2[6]), .Q(register_15_q), .clk(in_6));  // open: clr
  Register #(.width(16)) register_16 (.D(in_5), .en(Store_2[7]), .Q(register_16_q), .clk(in_6));  // open: clr
  assign out_7 = Bank_2A[7] ? register_9_q : 16'bz;  // Controlled_Buffer controlled_buffer_17
  assign out_8 = Bank_2B[7] ? register_9_q : 16'bz;  // Controlled_Buffer controlled_buffer_18
  assign out_7 = Bank_2A[6] ? register_10_q : 16'bz;  // Controlled_Buffer controlled_buffer_19
  assign out_8 = Bank_2B[6] ? register_10_q : 16'bz;  // Controlled_Buffer controlled_buffer_20
  assign out_7 = Bank_2A[5] ? register_11_q : 16'bz;  // Controlled_Buffer controlled_buffer_21
  assign out_8 = Bank_2B[5] ? register_11_q : 16'bz;  // Controlled_Buffer controlled_buffer_22
  assign out_7 = Bank_2A[4] ? register_12_q : 16'bz;  // Controlled_Buffer controlled_buffer_23
  assign out_8 = Bank_2B[4] ? register_12_q : 16'bz;  // Controlled_Buffer controlled_buffer_24
  assign out_7 = Bank_2A[3] ? register_13_q : 16'bz;  // Controlled_Buffer controlled_buffer_25
  assign out_8 = Bank_2B[3] ? register_13_q : 16'bz;  // Controlled_Buffer controlled_buffer_26
  assign out_7 = Bank_2A[2] ? register_14_q : 16'bz;  // Controlled_Buffer controlled_buffer_27
  assign out_8 = Bank_2B[2] ? register_14_q : 16'bz;  // Controlled_Buffer controlled_buffer_28
  assign out_7 = Bank_2A[1] ? register_15_q : 16'bz;  // Controlled_Buffer controlled_buffer_29
  assign out_8 = Bank_2B[1] ? register_15_q : 16'bz;  // Controlled_Buffer controlled_buffer_30
  assign out_7 = Bank_2A[0] ? register_16_q : 16'bz;  // Controlled_Buffer controlled_buffer_31
  assign out_8 = Bank_2B[0] ? register_16_q : 16'bz;  // Controlled_Buffer controlled_buffer_32
  assign out_7 = Bank_3A[7] ? register_17_q : 16'bz;  // Controlled_Buffer controlled_buffer_33
  Register #(.width(16)) register_17 (.D(in_5), .en(Store_3[0]), .Q(register_17_q), .clk(in_6));  // open: clr
  assign out_8 = Bank_3B[7] ? register_17_q : 16'bz;  // Controlled_Buffer controlled_buffer_34
  assign out_7 = Bank_3A[6] ? register_18_q : 16'bz;  // Controlled_Buffer controlled_buffer_35
  Register #(.width(16)) register_18 (.D(in_5), .en(Store_3[1]), .Q(register_18_q), .clk(in_6));  // open: clr
  assign out_8 = Bank_3B[6] ? register_18_q : 16'bz;  // Controlled_Buffer controlled_buffer_36
  assign out_7 = Bank_3A[5] ? register_19_q : 16'bz;  // Controlled_Buffer controlled_buffer_37
  Register #(.width(16)) register_19 (.D(in_5), .en(Store_3[2]), .Q(register_19_q), .clk(in_6));  // open: clr
  assign out_8 = Bank_3B[5] ? register_19_q : 16'bz;  // Controlled_Buffer controlled_buffer_38
  assign out_7 = Bank_3A[4] ? register_20_q : 16'bz;  // Controlled_Buffer controlled_buffer_39
  Register #(.width(16)) register_20 (.D(in_5), .en(Store_3[3]), .Q(register_20_q), .clk(in_6));  // open: clr
  assign out_8 = Bank_3B[4] ? register_20_q : 16'bz;  // Controlled_Buffer controlled_buffer_40
  assign out_7 = Bank_3A[3] ? register_21_q : 16'bz;  // Controlled_Buffer controlled_buffer_41
  Register #(.width(16)) register_21 (.D(in_5), .en(Store_3[4]), .Q(register_21_q), .clk(in_6));  // open: clr
  assign out_8 = Bank_3B[3] ? register_21_q : 16'bz;  // Controlled_Buffer controlled_buffer_42
  assign out_7 = Bank_3A[2] ? register_22_q : 16'bz;  // Controlled_Buffer controlled_buffer_43
  Register #(.width(16)) register_22 (.D(in_5), .en(Store_3[5]), .Q(register_22_q), .clk(in_6));  // open: clr
  assign out_8 = Bank_3B[2] ? register_22_q : 16'bz;  // Controlled_Buffer controlled_buffer_44
  assign out_7 = Bank_3A[1] ? register_23_q : 16'bz;  // Controlled_Buffer controlled_buffer_45
  Register #(.width(16)) register_23 (.D(in_5), .en(Store_3[6]), .Q(register_23_q), .clk(in_6));  // open: clr
  assign out_8 = Bank_3B[1] ? register_23_q : 16'bz;  // Controlled_Buffer controlled_buffer_46
  assign out_7 = Bank_3A[0] ? register_24_q : 16'bz;  // Controlled_Buffer controlled_buffer_47
  Register #(.width(16)) register_24 (.D(in_5), .en(Store_3[7]), .Q(register_24_q), .clk(in_6));  // open: clr
  assign out_8 = Bank_3B[0] ? register_24_q : 16'bz;  // Controlled_Buffer controlled_buffer_48
  assign out_7 = Bank_4A[7] ? register_25_q : 16'bz;  // Controlled_Buffer controlled_buffer_49
  Register #(.width(16)) register_25 (.D(in_5), .en(Store_4[0]), .Q(register_25_q), .clk(in_6));  // open: clr
  assign out_8 = Bank_4B[7] ? register_25_q : 16'bz;  // Controlled_Buffer controlled_buffer_50
  assign out_7 = Bank_4A[6] ? register_26_q : 16'bz;  // Controlled_Buffer controlled_buffer_51
  Register #(.width(16)) register_26 (.D(in_5), .en(Store_4[1]), .Q(register_26_q), .clk(in_6));  // open: clr
  assign out_8 = Bank_4B[6] ? register_26_q : 16'bz;  // Controlled_Buffer controlled_buffer_52
  assign out_7 = Bank_4A[5] ? register_27_q : 16'bz;  // Controlled_Buffer controlled_buffer_53
  Register #(.width(16)) register_27 (.D(in_5), .en(Store_4[2]), .Q(register_27_q), .clk(in_6));  // open: clr
  assign out_8 = Bank_4B[5] ? register_27_q : 16'bz;  // Controlled_Buffer controlled_buffer_54
  assign out_7 = Bank_4A[4] ? register_28_q : 16'bz;  // Controlled_Buffer controlled_buffer_55
  Register #(.width(16)) register_28 (.D(in_5), .en(Store_4[3]), .Q(register_28_q), .clk(in_6));  // open: clr
  assign out_8 = Bank_4B[4] ? register_28_q : 16'bz;  // Controlled_Buffer controlled_buffer_56
  assign out_7 = Bank_4A[3] ? register_29_q : 16'bz;  // Controlled_Buffer controlled_buffer_57
  Register #(.width(16)) register_29 (.D(in_5), .en(Store_4[4]), .Q(register_29_q), .clk(in_6));  // open: clr
  assign out_8 = Bank_4B[3] ? register_29_q : 16'bz;  // Controlled_Buffer controlled_buffer_58
  assign out_7 = Bank_4A[2] ? register_30_q : 16'bz;  // Controlled_Buffer controlled_buffer_59
  Register #(.width(16)) register_30 (.D(in_5), .en(Store_4[5]), .Q(register_30_q), .clk(in_6));  // open: clr
  assign out_8 = Bank_4B[2] ? register_30_q : 16'bz;  // Controlled_Buffer controlled_buffer_60
  assign out_7 = Bank_4A[1] ? register_31_q : 16'bz;  // Controlled_Buffer controlled_buffer_61
  Register #(.width(16)) register_31 (.D(in_5), .en(Store_4[6]), .Q(register_31_q), .clk(in_6));  // open: clr
  assign out_8 = Bank_4B[1] ? register_31_q : 16'bz;  // Controlled_Buffer controlled_buffer_62
  assign out_7 = Bank_4A[0] ? register_32_q : 16'bz;  // Controlled_Buffer controlled_buffer_63
  Register #(.width(16)) register_32 (.D(in_5), .en(Store_4[7]), .Q(register_32_q), .clk(in_6));  // open: clr
  assign out_8 = Bank_4B[0] ? register_32_q : 16'bz;  // Controlled_Buffer controlled_buffer_64

  // Other names for the same wires on the sheet: Clock = in_6; Data[15:0] = in_5; Output_A[15:0] = out_7;
  //   Output_B[15:0] = out_8
endmodule
